// Logisim project IT1601_U201614898_潘翔_CPU.circ as structural Verilog: 13 circuits, main circuit ◇多周期MIPS(微程序)
module \单周期MIPS_硬布线  (
  output [4:0] out_1,
  output [5:0] Op,
  output [4:0] out_3,
  output [31:0] out_4,
  output [4:0] out_5,
  output [31:0] out_6,
  output [5:0] Func,
  output [31:0] out_8,
  output [31:0] out_9,
  output [3:0] out_10,
  output [4:0] out_11,
  output [31:0] out_12,
  output [31:0] out_13,
  output [31:0] out_14,
  output [31:0] out_15
);

  wire and_1_out, and_2_out, CLK, MemWrite, not_1_out, not_2_out, or_1_out, RST, \单周期硬布线控制器_1_alusrc ,
       \单周期硬布线控制器_1_beq , \单周期硬布线控制器_1_bne , \单周期硬布线控制器_1_halt , \单周期硬布线控制器_1_memtoreg ,
       \单周期硬布线控制器_1_regdst , \单周期硬布线控制器_1_regwrite , \算术逻辑运算单元alu_2_equal ;
  wire [15:0] \总周期数 ;
  wire [15:6] rom_1_data;
  wire [31:0] multiplexer_1_out, multiplexer_3_out, ram_1_data, shifter_1_out;

  Button \u_总复位  (.out(RST));
  not not_1 (not_1_out, \单周期硬布线控制器_1_halt );
  Multiplexer #(.width(32)) multiplexer_1 (
    .in0(out_14), .in1(out_13), .out(multiplexer_1_out), .sel(or_1_out));  // open: en
  Register #(.width(32)) PC (.D(multiplexer_1_out), .en(not_1_out), .Q(out_6), .clk(CLK));  // open: clr
  Clock clock_1 (.out(CLK));
  \算术逻辑运算单元ALU  \u_算术逻辑运算单元alu_1  (
    .AluOP(4'b0101), .X(out_6), .Result(out_14), .Y(32'h4));  // open: Equal, Signed_Overflow, Result_2, UnSigned_Overflow
  ROM #(.addrWidth(10), .dataWidth(32)) rom_1 (
    .addr(out_6[11:2]), .data({Op, out_1, out_3, rom_1_data, Func}));  // open: sel
  // Mips_Probe mips_probe_1: pin names not known; wires that end beside it: {Op, out_1, out_3, rom_1_data, Func}
  // Probe on \总周期数 
  \单周期硬布线控制器  \u_单周期硬布线控制器_1  (
    .Func(Func), .RegWrite(\单周期硬布线控制器_1_regwrite ), .MemToReg(\单周期硬布线控制器_1_memtoreg ), .MemWrite(MemWrite),
    .Beq(\单周期硬布线控制器_1_beq ), .Bne(\单周期硬布线控制器_1_bne ), .RegDst(\单周期硬布线控制器_1_regdst ),
    .AluSrc(\单周期硬布线控制器_1_alusrc ), .ALU_OP(out_10), .OP(Op), .Halt(\单周期硬布线控制器_1_halt ));
  Multiplexer #(.width(5)) multiplexer_2 (
    .in0(out_3), .in1(rom_1_data[15:11]), .out(out_5), .sel(\单周期硬布线控制器_1_regdst ));  // open: en
  assign out_12 = {{16{rom_1_data[15]}}, {rom_1_data, Func}};  // Bit_Extender bit_extender_1
  MIPS_Regifile mips_regifile_1 (
    .Din(out_15), .Clk(CLK), .R1(out_8), .R2(out_9), .WE(\单周期硬布线控制器_1_regwrite ), .W_num(out_5),
    .R1_num(out_1), .R2_num(out_3));
  Multiplexer #(.width(32)) multiplexer_3 (
    .in0(out_9), .in1(out_12), .out(multiplexer_3_out), .sel(\单周期硬布线控制器_1_alusrc ));  // open: en
  Shifter #(.width(32)) shifter_1 (.in(out_12), .\dist (5'b00010), .out(shifter_1_out));
  and and_1 (and_1_out, \单周期硬布线控制器_1_beq , \算术逻辑运算单元alu_2_equal );
  not not_2 (not_2_out, \算术逻辑运算单元alu_2_equal );
  \算术逻辑运算单元ALU  \u_算术逻辑运算单元alu_2  (
    .AluOP(out_10), .X(out_8), .Equal(\算术逻辑运算单元alu_2_equal ), .Result(out_4), .Y(multiplexer_3_out));  // open: Signed_Overflow, Result_2, UnSigned_Overflow
  \算术逻辑运算单元ALU  \u_算术逻辑运算单元alu_3  (
    .AluOP(4'b0101), .X(shifter_1_out), .Result(out_13), .Y(out_14));  // open: Equal, Signed_Overflow, Result_2, UnSigned_Overflow
  Counter #(.width(16), .max('hffff)) counter_1 (
    .count(\单周期硬布线控制器_1_memtoreg ), .Q(\总周期数 ), .clk(CLK), .clr(RST));  // open: load, D, carry
  or or_1 (or_1_out, and_1_out, and_2_out);
  and and_2 (and_2_out, \单周期硬布线控制器_1_bne , not_2_out);
  RAM #(.addrWidth(10), .dataWidth(32), .bus("separate")) ram_1 (
    .addr(out_4[11:2]), .din(out_9), .data(ram_1_data), .str(MemWrite), .clk(CLK), .ld(1'b1));  // open: sel, clr
  Multiplexer #(.width(32)) multiplexer_4 (
    .in0(out_4), .in1(ram_1_data), .out(out_15), .sel(\单周期硬布线控制器_1_memtoreg ));  // open: en
  // RegisterFile registerfile_1: pin names not known
  Shifter #(.width(32)) shifter_2 ();  // open: in, dist, out

  assign out_11 = out_5;

  // Other names for the same wires on the sheet: R2_num[4:0] = out_3; R1_num[4:0] = out_1; R1[31:0] = out_8;
  //   R2[31:0] = out_9; RegDest[4:0] = out_5

  // Notes on the sheet:
  //   Ctrl+K  Command+K触发时钟连续仿真，程序运行结束后可停机，查看数据存储器中80单元的排序情况是有符号降序
  //   指令存储器
  //   contents of rom_1 (hex, n*v repeats v):
  //   2010ffff 20110000 ae300200 22100001 22310004 ae300200 22100001 22310004 ae300200 22100001 22310004
  //   ae300200 22100001 22310004 ae300200 22100001 22310004 ae300200 22100001 22310004 ae300200 22100001
  //   22310004 ae300200 8020 2011001c 8e130200 8e340200 274402a 11000002 ae330200 ae140200 2231fffc
  //   1611fff8 22100004 2011001c 1611fff5 2002000a c
  //   Halt
  //   Beq
  //   Bne
  //   RegDst
  //   MemToReg
  //   MemWrite
  //   AluOP
  //   AluSrcB
  //   RegWrite
endmodule

// 单周期硬布线控制器
module \单周期硬布线控制器  (
  input  [5:0] OP,
  input  [5:0] Func,
  output [3:0] ALU_OP,
  output RegDst,
  output RegWrite,
  output MemToReg,
  output MemWrite,
  output AluSrc,
  output Beq,
  output Bne,
  output Halt
);

  wire ADD, ADDI, comparator_6_eq, comparator_7_eq, comparator_8_eq, comparator_9_eq, or_4_out, SLT;

  Comparator #(.width(6)) comparator_1 (.a(OP), .b(6'b100011), .eq(MemToReg));  // open: gt, lt
  Comparator #(.width(6)) comparator_2 (.a(OP), .b(6'b101011), .eq(MemWrite));  // open: gt, lt
  Comparator #(.width(6)) comparator_3 (.a(OP), .b(6'b000100), .eq(Beq));  // open: gt, lt
  Comparator #(.width(6)) comparator_4 (.a(OP), .b(6'b000101), .eq(Bne));  // open: gt, lt
  Comparator #(.width(6)) comparator_5 (.a(OP), .b(6'b001000), .eq(ADDI));  // open: gt, lt
  Comparator #(.width(6)) comparator_6 (.a(OP), .b({6{1'b0}}), .eq(comparator_6_eq));  // open: gt, lt
  or or_1 (RegWrite, MemToReg, ADDI, RegDst);
  Comparator #(.width(6)) comparator_7 (.a(Func), .b(6'b100000), .eq(comparator_7_eq));  // open: gt, lt
  Comparator #(.width(6)) comparator_8 (.a(Func), .b(6'b101010), .eq(comparator_8_eq));  // open: gt, lt
  Comparator #(.width(6)) comparator_9 (.a(Func), .b(6'b001100), .eq(comparator_9_eq));  // open: gt, lt
  or or_2 (RegDst, ADD, SLT);
  and and_1 (ADD, comparator_7_eq, comparator_6_eq);
  and and_2 (SLT, comparator_8_eq, comparator_6_eq);
  and and_3 (Halt, comparator_9_eq, comparator_6_eq);
  or or_3 (AluSrc, MemWrite, MemToReg, ADDI);
  or or_4 (or_4_out, MemToReg, MemWrite, ADDI, ADD);
  Multiplexer #(.width(4), .enable("false")) multiplexer_1 (.in0(4'b1011), .in1(4'b0101), .out(ALU_OP), .sel(or_4_out));

  // Other names for the same wires on the sheet: LW = MemToReg; R_TYPE = RegDst; SW = MemWrite; SysCall = Halt

  // Notes on the sheet:
  //   指令译码信号
  //   指令译码逻辑
  //   给出简单的逻辑实现对应指令译码信号，LW、SW、BEQ、BNE、ADDI、ADD、SLT、SYSCALL、R_TYPE。
  //   ALU控制器逻辑
  //   注意R_TYPE表示R型运算指令，SYSCALL是特殊的R型指令，不属于这个类别
  //   根据指令译码信号实现控制器输出控制信号的逻辑
  //   给出简单的逻辑实现ALU_OP与OP、Func之间的对应关系
  //   控制信号
endmodule

module \多周期MIPS_微程序  (
  output [1:0] out_1,
  output [3:0] out_2,
  output [31:0] out_3,
  output [9:0] out_4,
  output [31:0] out_5
);

  wire and_1_out, and_2_out, CLK, MemRead, MemWrite, not_1_out, or_1_out, RST, \多周期微程序控制器_1_alusrca ,
       \多周期微程序控制器_1_beq , \多周期微程序控制器_1_bne , \多周期微程序控制器_1_iord , \多周期微程序控制器_1_irwrite ,
       \多周期微程序控制器_1_memtoreg , \多周期微程序控制器_1_pcsrc , \多周期微程序控制器_1_pcwrite , \多周期微程序控制器_1_regdst ,
       \多周期微程序控制器_1_regwrite , \算术逻辑运算单元alu_1_equal ;
  wire [3:0] \多周期微程序控制器_1_当前微指令地址 ;
  wire [4:0] multiplexer_2_out;
  wire [15:0] \总周期数 ;
  wire [31:0] A_q, B_q, bit_extender_1_out, C_q, DR_q, IR_q, mips_probe_1_p1, mips_regifile_1_r1,
       mips_regifile_1_r2, multiplexer_1_out, multiplexer_3_out, multiplexer_4_out, PC_q, shifter_1_out,
       \算术逻辑运算单元alu_1_result ;

  Button \u_总复位  (.out(RST));
  Register #(.width(32)) PC (.D(out_5), .en(or_1_out), .Q(PC_q), .clk(CLK), .clr(RST));
  Clock clock_1 (.out(CLK));
  Counter #(.width(16), .max('hffff)) counter_1 (
    .count(or_1_out), .Q(\总周期数 ), .clk(CLK), .clr(RST));  // open: load, D, carry
  Multiplexer #(.width(32)) multiplexer_1 (
    .in0(PC_q), .in1(C_q), .out({multiplexer_1_out[31:12], out_4, multiplexer_1_out[1:0]}),
    .sel(\多周期微程序控制器_1_iord ));  // open: en
  // Mips_Probe mips_probe_1: pin names not known; wires that end beside it: mips_probe_1_p1
  RAM #(.addrWidth(10), .dataWidth(32), .bus("separate")) ram_1 (
    .addr(out_4), .din(B_q), .data(mips_probe_1_p1), .str(MemWrite), .clk(CLK), .ld(MemRead));  // open: sel, clr
  // Probe on \总周期数 
  Register #(.width(32)) IR (.D(mips_probe_1_p1), .en(\多周期微程序控制器_1_irwrite ), .Q(IR_q), .clk(CLK));  // open: clr
  Register #(.width(32)) DR (.D(mips_probe_1_p1), .Q(DR_q), .clk(CLK));  // open: en, clr
  // Probe on \多周期微程序控制器_1_当前微指令地址 
  assign bit_extender_1_out = {{16{IR_q[15]}}, IR_q[15:0]};  // Bit_Extender bit_extender_1
  \多周期微程序控制器  \u_多周期微程序控制器_1  (
    .PcWrite(\多周期微程序控制器_1_pcwrite ), .Beq(\多周期微程序控制器_1_beq ), .PCsrc(\多周期微程序控制器_1_pcsrc ), .AluSrcB(out_1),
    .AluSrcA(\多周期微程序控制器_1_alusrca ), .RegWrite(\多周期微程序控制器_1_regwrite ), .MemToReg(\多周期微程序控制器_1_memtoreg ),
    .RegDst(\多周期微程序控制器_1_regdst ), .IorD(\多周期微程序控制器_1_iord ), .MemWrite(MemWrite), .MemRead(MemRead),
    .IrWrite(\多周期微程序控制器_1_irwrite ), .Bne(\多周期微程序控制器_1_bne ), .CLK(CLK), .\当前微指令地址 (\多周期微程序控制器_1_当前微指令地址 ),
    .RST(RST), .OP(IR_q[31:26]), .ALU_OP(out_2), .Func(IR_q[5:0]));
  Multiplexer #(.width(5)) multiplexer_2 (
    .in0(IR_q[20:16]), .in1(IR_q[15:11]), .out(multiplexer_2_out), .sel(\多周期微程序控制器_1_regdst ));  // open: en
  Multiplexer #(.width(32)) multiplexer_3 (
    .in0(C_q), .in1(DR_q), .out(multiplexer_3_out), .sel(\多周期微程序控制器_1_memtoreg ));  // open: en
  MIPS_Regifile mips_regifile_1 (
    .Din(multiplexer_3_out), .Clk(CLK), .R1(mips_regifile_1_r1), .R2(mips_regifile_1_r2),
    .WE(\多周期微程序控制器_1_regwrite ), .W_num(multiplexer_2_out), .R1_num(IR_q[25:21]), .R2_num(IR_q[20:16]));
  Register #(.width(32)) A (.D(mips_regifile_1_r1), .Q(A_q), .clk(CLK));  // open: en, clr
  Register #(.width(32)) B (.D(mips_regifile_1_r2), .Q(B_q), .clk(CLK));  // open: en, clr
  Multiplexer #(.width(32)) multiplexer_4 (
    .in0(PC_q), .in1(A_q), .out(multiplexer_4_out), .sel(\多周期微程序控制器_1_alusrca ));  // open: en
  Shifter #(.width(32)) shifter_1 (.in(bit_extender_1_out), .\dist (5'b00010), .out(shifter_1_out));
  Multiplexer #(.select(2), .width(32)) multiplexer_5 (
    .in0(B_q), .in1(32'h4), .in2(bit_extender_1_out), .in3(shifter_1_out), .out(out_3), .sel(out_1));  // open: en
  \算术逻辑运算单元ALU  \u_算术逻辑运算单元alu_1  (
    .AluOP(out_2), .X(multiplexer_4_out), .Equal(\算术逻辑运算单元alu_1_equal ), .Result(\算术逻辑运算单元alu_1_result ),
    .Y(out_3));  // open: Signed_Overflow, Result_2, UnSigned_Overflow
  not not_1 (not_1_out, \算术逻辑运算单元alu_1_equal );
  Register #(.width(32)) C (.D(\算术逻辑运算单元alu_1_result ), .Q(C_q), .clk(CLK));  // open: en, clr
  and and_1 (and_1_out, \多周期微程序控制器_1_beq , \算术逻辑运算单元alu_1_equal );
  and and_2 (and_2_out, not_1_out, \多周期微程序控制器_1_bne );
  or or_1 (or_1_out, \多周期微程序控制器_1_pcwrite , and_1_out, and_2_out);
  Multiplexer #(.width(32)) multiplexer_6 (
    .in0(\算术逻辑运算单元alu_1_result ), .in1(C_q), .out(out_5), .sel(\多周期微程序控制器_1_pcsrc ));  // open: en

  // Other names for the same wires on the sheet: Addr[9:0] = out_4

  // Notes on the sheet:
  //   Ctrl+K  Command+K触发时钟连续仿真，程序运行结束后可停机，查看数据存储器中80单元的排序情况是有符号降序
  //   存储器
  //   IorD
  //   MemWrite
  //   MemRead
  //   IRWrite
  //   OP
  //   Func
  //   RegDst
  //   PcWrite
  //   Beq
  //   Bne
  //   PcSrc
  //   AluOP
  //   AluSrcB
  //   AluSrcA
  //   RegWrite
  //   MemToReg
endmodule

// 微程序控制器
module \多周期微程序控制器  (
  input  [5:0] OP,
  input  [5:0] Func,
  input  CLK,
  input  RST,
  output [3:0] ALU_OP,
  output Bne,
  output Beq,
  output MemRead,
  output MemWrite,
  output RegWrite,
  output PcWrite,
  output IrWrite,
  output RegDst,
  output MemToReg,
  output [3:0] \当前微指令地址 ,
  output [1:0] AluSrcB,
  output AluSrcA,
  output PCsrc,
  output IorD
);

  wire ADD, ADDI, BEQ_t, BNE_t, comparator_6_eq, comparator_7_eq, comparator_8_eq, comparator_9_eq, LW, P,
       R_TYPE, SLT, SW, SysCall;
  wire [1:0] ALU_Control;
  wire [3:0] multiplexer_1_out, multiplexer_2_out, rom_1_data, \微程序地址转移逻辑_1_s0 ;

  Comparator #(.width(6)) comparator_1 (.a(OP), .b(6'b100011), .eq(LW));  // open: gt, lt
  Comparator #(.width(6)) comparator_2 (.a(OP), .b(6'b101011), .eq(SW));  // open: gt, lt
  Comparator #(.width(6)) comparator_3 (.a(OP), .b(6'b000100), .eq(BEQ_t));  // open: gt, lt
  Comparator #(.width(6)) comparator_4 (.a(OP), .b(6'b000101), .eq(BNE_t));  // open: gt, lt
  Comparator #(.width(6)) comparator_5 (.a(OP), .b(6'b001000), .eq(ADDI));  // open: gt, lt
  Comparator #(.width(6)) comparator_6 (.a(OP), .b({6{1'b0}}), .eq(comparator_6_eq));  // open: gt, lt
  \微程序地址转移逻辑  \u_微程序地址转移逻辑_1  (
    .R_Type(R_TYPE), .S3(\微程序地址转移逻辑_1_s0 [3]), .ADDI(ADDI), .S2(\微程序地址转移逻辑_1_s0 [2]), .LW(LW),
    .S1(\微程序地址转移逻辑_1_s0 [1]), .SW(SW), .S0(\微程序地址转移逻辑_1_s0 [0]), .BEQ(BEQ_t), .BNE(BNE_t), .SYSCALL(SysCall));
  Comparator #(.width(6)) comparator_7 (.a(Func), .b(6'b100000), .eq(comparator_7_eq));  // open: gt, lt
  Comparator #(.width(6)) comparator_8 (.a(Func), .b(6'b101010), .eq(comparator_8_eq));  // open: gt, lt
  Comparator #(.width(6)) comparator_9 (.a(Func), .b(6'b001100), .eq(comparator_9_eq));  // open: gt, lt
  and and_1 (ADD, comparator_7_eq, comparator_6_eq);
  and and_2 (SLT, comparator_8_eq, comparator_6_eq);
  and and_3 (SysCall, comparator_9_eq, comparator_6_eq);
  Register #(.width(4)) register_1 (.D(multiplexer_1_out), .Q(\当前微指令地址 ), .clk(CLK), .clr(RST));  // open: en
  Multiplexer #(.width(4), .enable("false")) multiplexer_1 (
    .in0(rom_1_data), .in1(\微程序地址转移逻辑_1_s0 ), .out(multiplexer_1_out), .sel(P));
  or or_1 (R_TYPE, ADD, SLT);
  ROM #(.addrWidth(4), .dataWidth(21)) rom_1 (
    .addr(\当前微指令地址 ),
    .data({IorD, PCsrc, AluSrcA, AluSrcB, MemToReg, RegDst, IrWrite, PcWrite, RegWrite, MemWrite, MemRead, Beq, Bne, ALU_Control, P, rom_1_data}));  // open: sel
  Multiplexer #(.width(4)) multiplexer_2 (
    .in0(4'b0101), .in1(4'b1011), .out(multiplexer_2_out), .sel(SLT));  // open: en
  Multiplexer #(.select(2), .width(4), .enable("false")) multiplexer_3 (
    .in0(4'b0101), .in1(4'b0110), .in2(multiplexer_2_out), .out(ALU_OP), .sel(ALU_Control));  // open: in3

  // Notes on the sheet:
  //   指令译码信号
  //   根据指令进行微程序地址转移
  //   指令译码逻辑
  //   给出简单的逻辑实现对应指令译码信号，LW、SW、BEQ、BNE、ADDI、ADD、SLT、SYSCALL、R_TYPE。
  //   下址字段
  //   微程序入口地址
  //   判断逻辑
  //   μAR
  //   微程序控制器
  //   contents of rom_1 (hex, n*v repeats v):
  //   13201 30010 60003 130204 38800 60006 130400 40048 34800 c0100 c0080 6000c 30800 3000d
  //   微命令
  //   ALU控制器逻辑
  //   根据ALU_Control的值决定运算器运算选择控制信号ALU_OP的值
  //   注意R_TYPE表示R型运算指令，SYSCALL是特殊的R型指令，不属于这个类别
  //   微指令
  //   下址字段
  //   判断逻辑
  //   ALU_Control= 00 运算器做加法
  //   ALU_Control= 01 运算器做减法
  //   ALU_Control= 10 运算方式由Func决定 
endmodule

// 地址转移逻辑
module \微程序地址转移逻辑  (
  input  R_Type,
  input  ADDI,
  input  LW,
  input  SW,
  input  BEQ,
  input  BNE,
  input  SYSCALL,
  output S3,
  output S2,
  output S1,
  output S0
);

  or or_1 (S3, ADDI, BEQ, BNE, SYSCALL);
  or or_2 (S2, R_Type, SW, SYSCALL);
  or or_3 (S1, R_Type, ADDI, LW, BNE);
  or or_4 (S0, R_Type, ADDI, SW, BEQ, SYSCALL);
endmodule

module \多周期MIPS_硬布线  (
  output [1:0] out_1,
  output [31:0] out_2,
  output [31:0] out_3,
  output [9:0] out_4,
  output [31:0] out_5
);

  wire and_1_out, and_2_out, CLK, MemRead, MemWrite, not_1_out, or_1_out, RST, \多周期硬布线控制器_1_alusrca ,
       \多周期硬布线控制器_1_beq , \多周期硬布线控制器_1_bne , \多周期硬布线控制器_1_iord , \多周期硬布线控制器_1_irwrite ,
       \多周期硬布线控制器_1_memtoreg , \多周期硬布线控制器_1_pcsrc , \多周期硬布线控制器_1_pcwrite , \多周期硬布线控制器_1_regdst ,
       \多周期硬布线控制器_1_regwrite , \算术逻辑运算单元alu_1_equal ;
  wire [3:0] \多周期硬布线控制器_1_alu_op , \多周期硬布线控制器_1_当前状态 ;
  wire [4:0] multiplexer_2_out;
  wire [15:0] \总周期数 ;
  wire [31:0] A_q, B_q, bit_extender_1_out, C_q, DR_q, IR_q, mips_probe_1_p1, mips_regifile_1_r1,
       mips_regifile_1_r2, multiplexer_1_out, multiplexer_3_out, multiplexer_4_out, PC_q, shifter_1_out;

  Button \u_总复位  (.out(RST));
  Register #(.width(32)) PC (.D(out_5), .en(or_1_out), .Q(PC_q), .clk(CLK), .clr(RST));
  Clock clock_1 (.out(CLK));
  Counter #(.width(16), .max('hffff)) counter_1 (
    .count(or_1_out), .Q(\总周期数 ), .clk(CLK), .clr(RST));  // open: load, D, carry
  Multiplexer #(.width(32)) multiplexer_1 (
    .in0(PC_q), .in1(C_q), .out({multiplexer_1_out[31:12], out_4, multiplexer_1_out[1:0]}),
    .sel(\多周期硬布线控制器_1_iord ));  // open: en
  // Mips_Probe mips_probe_1: pin names not known; wires that end beside it: mips_probe_1_p1
  RAM #(.addrWidth(10), .dataWidth(32), .bus("separate")) ram_1 (
    .addr(out_4), .din(B_q), .data(mips_probe_1_p1), .str(MemWrite), .clk(CLK), .ld(MemRead));  // open: sel, clr
  // Probe on \总周期数 
  Register #(.width(32)) IR (.D(mips_probe_1_p1), .en(\多周期硬布线控制器_1_irwrite ), .Q(IR_q), .clk(CLK));  // open: clr
  Register #(.width(32)) DR (.D(mips_probe_1_p1), .Q(DR_q), .clk(CLK));  // open: en, clr
  // Probe on \多周期硬布线控制器_1_当前状态 
  assign bit_extender_1_out = {{16{IR_q[15]}}, IR_q[15:0]};  // Bit_Extender bit_extender_1
  \多周期硬布线控制器  \u_多周期硬布线控制器_1  (
    .RST(RST), .AluSrcB(out_1), .OP(IR_q[31:26]), .CLK(CLK), .\当前状态 (\多周期硬布线控制器_1_当前状态 ),
    .IorD(\多周期硬布线控制器_1_iord ), .PCsrc(\多周期硬布线控制器_1_pcsrc ), .AluSrcA(\多周期硬布线控制器_1_alusrca ),
    .MemToReg(\多周期硬布线控制器_1_memtoreg ), .RegDst(\多周期硬布线控制器_1_regdst ), .IrWrite(\多周期硬布线控制器_1_irwrite ),
    .PcWrite(\多周期硬布线控制器_1_pcwrite ), .RegWrite(\多周期硬布线控制器_1_regwrite ), .MemWrite(MemWrite),
    .MemRead(MemRead), .Beq(\多周期硬布线控制器_1_beq ), .Bne(\多周期硬布线控制器_1_bne ), .Func(IR_q[5:0]),
    .ALU_OP(\多周期硬布线控制器_1_alu_op ));
  Multiplexer #(.width(5)) multiplexer_2 (
    .in0(IR_q[20:16]), .in1(IR_q[15:11]), .out(multiplexer_2_out), .sel(\多周期硬布线控制器_1_regdst ));  // open: en
  Multiplexer #(.width(32)) multiplexer_3 (
    .in0(C_q), .in1(DR_q), .out(multiplexer_3_out), .sel(\多周期硬布线控制器_1_memtoreg ));  // open: en
  Register #(.width(32)) A (.D(mips_regifile_1_r1), .Q(A_q), .clk(CLK));  // open: en, clr
  MIPS_Regifile mips_regifile_1 (
    .Din(multiplexer_3_out), .Clk(CLK), .R1(mips_regifile_1_r1), .R2(mips_regifile_1_r2),
    .WE(\多周期硬布线控制器_1_regwrite ), .W_num(multiplexer_2_out), .R1_num(IR_q[25:21]), .R2_num(IR_q[20:16]));
  Register #(.width(32)) B (.D(mips_regifile_1_r2), .Q(B_q), .clk(CLK));  // open: en, clr
  Multiplexer #(.width(32)) multiplexer_4 (
    .in0(PC_q), .in1(A_q), .out(multiplexer_4_out), .sel(\多周期硬布线控制器_1_alusrca ));  // open: en
  Shifter #(.width(32)) shifter_1 (.in(bit_extender_1_out), .\dist (5'b00010), .out(shifter_1_out));
  Multiplexer #(.select(2), .width(32)) multiplexer_5 (
    .in0(B_q), .in1(32'h4), .in2(bit_extender_1_out), .in3(shifter_1_out), .out(out_3), .sel(out_1));  // open: en
  \算术逻辑运算单元ALU  \u_算术逻辑运算单元alu_1  (
    .AluOP(\多周期硬布线控制器_1_alu_op ), .X(multiplexer_4_out), .Equal(\算术逻辑运算单元alu_1_equal ), .Result(out_2),
    .Y(out_3));  // open: Signed_Overflow, Result_2, UnSigned_Overflow
  not not_1 (not_1_out, \算术逻辑运算单元alu_1_equal );
  Register #(.width(32)) C (.D(out_2), .Q(C_q), .clk(CLK));  // open: en, clr
  and and_1 (and_1_out, \多周期硬布线控制器_1_beq , \算术逻辑运算单元alu_1_equal );
  and and_2 (and_2_out, not_1_out, \多周期硬布线控制器_1_bne );
  or or_1 (or_1_out, \多周期硬布线控制器_1_pcwrite , and_1_out, and_2_out);
  Multiplexer #(.width(32)) multiplexer_6 (.in0(out_2), .in1(C_q), .out(out_5), .sel(\多周期硬布线控制器_1_pcsrc ));  // open: en

  // Other names for the same wires on the sheet: Addr[9:0] = out_4

  // Notes on the sheet:
  //   Ctrl+K  Command+K触发时钟连续仿真，程序运行结束后可停机，查看数据存储器中80单元的排序情况是有符号降序
  //   完成微程序模式的多周期CPU后，将主机架构图复制到本电路中，替换控制器为硬布线控制器
  //   存储器
  //   IorD
  //   MemWrite
  //   MemRead
  //   IRWrite
  //   OP
  //   Func
  //   RegDst
  //   PcWrite
  //   Beq
  //   Bne
  //   PcSrc
  //   AluOP
  //   AluSrcB
  //   AluSrcA
  //   RegWrite
  //   MemToReg
endmodule

// 硬布线控制器
module \多周期硬布线控制器  (
  input  [5:0] OP,
  input  [5:0] Func,
  input  CLK,
  input  RST,
  output [3:0] ALU_OP,
  output Bne,
  output Beq,
  output MemRead,
  output MemWrite,
  output RegWrite,
  output PcWrite,
  output IrWrite,
  output RegDst,
  output MemToReg,
  output [3:0] \当前状态 ,
  output [1:0] AluSrcB,
  output AluSrcA,
  output PCsrc,
  output IorD
);

  wire ADD, ADDI, BEQ_t, BNE_t, comparator_6_eq, comparator_7_eq, comparator_8_eq, comparator_9_eq, LW, P,
       R_TYPE, SLT, SW, SysCall;
  wire [1:0] ALU_Control;
  wire [3:0] multiplexer_1_out, rom_1_data, \状态机fsm_1_n0 ;

  Comparator #(.width(6)) comparator_1 (.a(OP), .b(6'b100011), .eq(LW));  // open: gt, lt
  Comparator #(.width(6)) comparator_2 (.a(OP), .b(6'b101011), .eq(SW));  // open: gt, lt
  Comparator #(.width(6)) comparator_3 (.a(OP), .b(6'b000100), .eq(BEQ_t));  // open: gt, lt
  Comparator #(.width(6)) comparator_4 (.a(OP), .b(6'b000101), .eq(BNE_t));  // open: gt, lt
  Comparator #(.width(6)) comparator_5 (.a(OP), .b(6'b001000), .eq(ADDI));  // open: gt, lt
  Comparator #(.width(6)) comparator_6 (.a(OP), .b({6{1'b0}}), .eq(comparator_6_eq));  // open: gt, lt
  \状态机FSM  \u_状态机fsm_1  (
    .S3(\当前状态 [3]), .S2(\当前状态 [2]), .S1(\当前状态 [1]), .S0(\当前状态 [0]), .R_Type(R_TYPE), .ADDI(ADDI), .LW(LW),
    .N3(\状态机fsm_1_n0 [3]), .SW(SW), .BEQ(BEQ_t), .BNE(BNE_t), .SYSCALL(SysCall), .N2(\状态机fsm_1_n0 [2]),
    .N1(\状态机fsm_1_n0 [1]), .N0(\状态机fsm_1_n0 [0]));
  Comparator #(.width(6)) comparator_7 (.a(Func), .b(6'b100000), .eq(comparator_7_eq));  // open: gt, lt
  Comparator #(.width(6)) comparator_8 (.a(Func), .b(6'b101010), .eq(comparator_8_eq));  // open: gt, lt
  Comparator #(.width(6)) comparator_9 (.a(Func), .b(6'b001100), .eq(comparator_9_eq));  // open: gt, lt
  Register #(.width(4)) register_1 (.D(\状态机fsm_1_n0 ), .Q(\当前状态 ), .clk(CLK), .clr(RST));  // open: en
  or or_1 (R_TYPE, ADD, SLT);
  and and_1 (ADD, comparator_7_eq, comparator_6_eq);
  and and_2 (SLT, comparator_8_eq, comparator_6_eq);
  and and_3 (SysCall, comparator_9_eq, comparator_6_eq);
  ROM #(.addrWidth(4), .dataWidth(21)) rom_1 (
    .addr(\当前状态 ),
    .data({IorD, PCsrc, AluSrcA, AluSrcB, MemToReg, RegDst, IrWrite, PcWrite, RegWrite, MemWrite, MemRead, Beq, Bne, ALU_Control, P, rom_1_data}));  // open: sel
  Multiplexer #(.width(4)) multiplexer_1 (
    .in0(4'b0101), .in1(4'b1011), .out(multiplexer_1_out), .sel(SLT));  // open: en
  Multiplexer #(.select(2), .width(4), .enable("false")) multiplexer_2 (
    .in0(4'b0101), .in1(4'b0110), .in2(multiplexer_1_out), .out(ALU_OP), .sel(ALU_Control));  // open: in3

  // Notes on the sheet:
  //   指令译码信号
  //   现态
  //   组合逻辑
  //   指令译码逻辑
  //   次态
  //   状态寄存器
  //   微程序控制器
  //   contents of rom_1 (hex, n*v repeats v):
  //   13201 30010 60003 100204 8800 60006 100400 40048 4800 c0120 c00a0 6000c 800 d
  //   ALU控制器逻辑
  //   根据ALU_Control的值决定运算器运算选择控制信号ALU_OP的值
  //   ALU_Control= 00 运算器做加法
  //   ALU_Control= 01 运算器做减法
  //   ALU_Control= 10 运算方式由Func决定 
endmodule

// 控制器状态机
module \状态机FSM  (
  input  S3,
  input  S2,
  input  S1,
  input  S0,
  input  R_Type,
  input  ADDI,
  input  LW,
  input  SW,
  input  BEQ,
  input  BNE,
  input  SYSCALL,
  output N3,
  output N2,
  output N1,
  output N0
);

  wire and_1_out, and_2_out, and_3_out, and_4_out, and_5_out, and_6_out, and_7_out, and_8_out, and_9_out,
       and_10_out, and_11_out, and_12_out, and_13_out, and_14_out, and_15_out, and_16_out, and_17_out,
       and_18_out, and_19_out, and_20_out, and_21_out, and_22_out, and_23_out, and_24_out, and_25_out,
       and_26_out, and_27_out, and_28_out, not_1_out, not_2_out, not_3_out, not_4_out, not_5_out, not_6_out,
       not_7_out, not_8_out, not_9_out, not_10_out, not_11_out, not_12_out, not_13_out, not_14_out,
       not_15_out, not_16_out, not_17_out, not_18_out, not_19_out, not_20_out, not_21_out, not_22_out,
       not_23_out, not_24_out, not_25_out, not_26_out, not_27_out, not_28_out, not_29_out, not_30_out,
       not_31_out, not_32_out, not_33_out, not_34_out, not_35_out, not_36_out, not_37_out, not_38_out,
       not_39_out, not_40_out, not_41_out, not_42_out, not_43_out, not_44_out, not_45_out, not_46_out,
       not_47_out, not_48_out, not_49_out, not_50_out, not_51_out, not_52_out, not_53_out, not_54_out,
       not_55_out, not_56_out, not_57_out, not_58_out, not_59_out, not_60_out, not_61_out, not_62_out,
       not_63_out, not_64_out, not_65_out, not_66_out, not_67_out, not_68_out, not_69_out, not_70_out;

  not not_1 (not_1_out, S3);
  not not_2 (not_2_out, S2);
  not not_3 (not_3_out, S1);
  not not_4 (not_4_out, S3);
  not not_5 (not_5_out, S2);
  not not_6 (not_6_out, S1);
  not not_7 (not_7_out, S3);
  not not_8 (not_8_out, S2);
  not not_9 (not_9_out, S1);
  not not_10 (not_10_out, S3);
  not not_11 (not_11_out, S2);
  not not_12 (not_12_out, S1);
  not not_13 (not_13_out, S3);
  not not_14 (not_14_out, S2);
  not not_15 (not_15_out, S1);
  not not_16 (not_16_out, S3);
  not not_17 (not_17_out, S2);
  not not_18 (not_18_out, S1);
  not not_19 (not_19_out, S3);
  not not_20 (not_20_out, S2);
  not not_21 (not_21_out, S1);
  not not_22 (not_22_out, S3);
  not not_23 (not_23_out, S2);
  not not_24 (not_24_out, S1);
  not not_25 (not_25_out, S3);
  not not_26 (not_26_out, S2);
  not not_27 (not_27_out, S3);
  not not_28 (not_28_out, S1);
  not not_29 (not_29_out, S2);
  not not_30 (not_30_out, S1);
  not not_31 (not_31_out, S3);
  not not_32 (not_32_out, S2);
  not not_33 (not_33_out, S1);
  not not_34 (not_34_out, S3);
  not not_35 (not_35_out, S2);
  not not_36 (not_36_out, S1);
  not not_37 (not_37_out, S3);
  not not_38 (not_38_out, S2);
  not not_39 (not_39_out, S1);
  not not_40 (not_40_out, S3);
  not not_41 (not_41_out, S2);
  not not_42 (not_42_out, S1);
  not not_43 (not_43_out, S3);
  not not_44 (not_44_out, S2);
  not not_45 (not_45_out, S0);
  not not_46 (not_46_out, S3);
  not not_47 (not_47_out, S1);
  not not_48 (not_48_out, S3);
  not not_49 (not_49_out, S2);
  not not_50 (not_50_out, S1);
  not not_51 (not_51_out, S0);
  not not_52 (not_52_out, S3);
  not not_53 (not_53_out, S2);
  not not_54 (not_54_out, S1);
  not not_55 (not_55_out, S3);
  not not_56 (not_56_out, S2);
  not not_57 (not_57_out, S1);
  not not_58 (not_58_out, S3);
  not not_59 (not_59_out, S2);
  not not_60 (not_60_out, S1);
  not not_61 (not_61_out, S3);
  not not_62 (not_62_out, S2);
  not not_63 (not_63_out, S1);
  not not_64 (not_64_out, S3);
  not not_65 (not_65_out, S2);
  not not_66 (not_66_out, S1);
  not not_67 (not_67_out, S3);
  not not_68 (not_68_out, S2);
  not not_69 (not_69_out, S0);
  not not_70 (not_70_out, S1);
  and and_1 (and_1_out, not_1_out, not_2_out, not_3_out, S0, BEQ);
  and and_2 (and_2_out, not_4_out, not_5_out, not_6_out, S0, BNE);
  and and_3 (and_3_out, not_7_out, not_8_out, not_9_out, S0, SYSCALL);
  and and_4 (and_4_out, not_10_out, not_11_out, not_12_out, S0, ADDI);
  and and_5 (and_5_out, not_13_out, S2, S1, S0);
  and and_6 (and_6_out, S3, not_14_out, S1, S0);
  and and_7 (and_7_out, S3, S2, not_15_out, S0);
  and and_8 (and_8_out, not_16_out, not_17_out, not_18_out, S0, R_Type);
  and and_9 (and_9_out, not_19_out, not_20_out, not_21_out, S0, SW);
  and and_10 (and_10_out, not_22_out, not_23_out, not_24_out, S0, SYSCALL);
  and and_11 (and_11_out, not_25_out, not_26_out, S1, S0);
  and and_12 (and_12_out, not_27_out, S2, not_28_out, S0);
  and and_13 (and_13_out, S3, not_29_out, S1, S0);
  and and_14 (and_14_out, S3, S2, not_30_out, S0);
  and and_15 (and_15_out, not_31_out, not_32_out, not_33_out, S0, R_Type);
  and and_16 (and_16_out, not_34_out, not_35_out, not_36_out, S0, LW);
  and and_17 (and_17_out, not_37_out, not_38_out, not_39_out, S0, BNE);
  and and_18 (and_18_out, not_40_out, not_41_out, not_42_out, S0, ADDI);
  and and_19 (and_19_out, not_43_out, not_44_out, S1, not_45_out);
  and and_20 (and_20_out, not_46_out, S2, not_47_out, S0);
  and and_21 (and_21_out, not_48_out, not_49_out, not_50_out, not_51_out);
  and and_22 (and_22_out, not_52_out, not_53_out, not_54_out, S0, R_Type);
  and and_23 (and_23_out, not_55_out, not_56_out, not_57_out, S0, SW);
  and and_24 (and_24_out, not_58_out, not_59_out, not_60_out, S0, BEQ);
  and and_25 (and_25_out, not_61_out, not_62_out, not_63_out, S0, SYSCALL);
  and and_26 (and_26_out, not_64_out, not_65_out, not_66_out, S0, ADDI);
  and and_27 (and_27_out, not_67_out, not_68_out, S1, not_69_out);
  and and_28 (and_28_out, S3, S2, not_70_out, S0);
  or or_1 (N3, and_1_out, and_2_out, and_3_out, and_4_out, and_5_out, and_6_out, and_7_out);
  or or_2 (N2, and_8_out, and_9_out, and_10_out, and_11_out, and_12_out, and_13_out, and_14_out);
  or or_3 (N1, and_15_out, and_16_out, and_17_out, and_18_out, and_19_out, and_20_out);
  or or_4 (N0, and_21_out, and_22_out, and_23_out, and_24_out, and_25_out, and_26_out, and_27_out, and_28_out);
endmodule

module MIPS_Regifile (
  input  [31:0] Din,
  input  Clk,
  input  WE,
  input  [4:0] W_num,
  input  [4:0] R1_num,
  input  [4:0] R2_num,
  output [31:0] R1,
  output [31:0] R2
);

  // RegisterFile registerfile_1: pin names not known; wires that end beside it: Din, Clk, WE, W_num, R1_num, R2_num, R1, R2
endmodule

// ALU
module MIPS_ALU (
  input  [31:0] X,
  input  [31:0] Y,
  input  [3:0] AluOP,
  output Equal,
  output [31:0] Result,
  output [31:0] Result_2
);

  wire [0:0] comparator_1_lt, comparator_2_lt;
  wire [31:0] adder_1_out, AND_out, divider_1_out, divider_1_rem, multiplier_1_cout, multiplier_1_out,
       NOR_out, OR_out, shifter_1_out, shifter_2_out, shifter_3_out, subtractor_1_out, XOR_out;

  Shifter #(.width(32)) shifter_1 (.in(X), .\dist (Y[4:0]), .out(shifter_1_out));
  Shifter #(.width(32), .shift("ar")) shifter_2 (.in(X), .\dist (Y[4:0]), .out(shifter_2_out));
  Shifter #(.width(32), .shift("lr")) shifter_3 (.in(X), .\dist (Y[4:0]), .out(shifter_3_out));
  Multiplier #(.width(32)) multiplier_1 (.a(X), .b(Y), .out(multiplier_1_out), .cout(multiplier_1_cout));  // open: cin
  Divider #(.width(32)) divider_1 (.a(X), .b(Y), .out(divider_1_out), .rem(divider_1_rem));  // open: upper
  Adder #(.width(32)) adder_1 (.a(X), .b(Y), .out(adder_1_out));  // open: cin, cout
  Subtractor #(.width(32)) subtractor_1 (.a(X), .b(Y), .out(subtractor_1_out));  // open: bin, bout
  assign AND_out = X & Y;  // AND_Gate AND, 32 bits wide
  assign OR_out = X | Y;  // OR_Gate OR, 32 bits wide
  assign XOR_out = X ^ Y;  // XOR_Gate XOR, 32 bits wide
  assign NOR_out = ~(X | Y);  // NOR_Gate NOR, 32 bits wide
  Comparator #(.width(32)) comparator_1 (.a(X), .b(Y), .eq(Equal), .lt(comparator_1_lt[0]));  // open: gt
  Comparator #(.width(32)) comparator_2 (.a(X), .b(Y), .lt(comparator_2_lt[0]));  // open: gt, eq
  Multiplexer #(.select(4), .width(32), .enable("false")) multiplexer_1 (
    .in0(shifter_1_out), .in1(shifter_2_out), .in2(shifter_3_out), .in3(multiplier_1_out),
    .in4(divider_1_out), .in5(adder_1_out), .in6(subtractor_1_out), .in7(AND_out), .in8(OR_out),
    .in9(XOR_out), .in10(NOR_out), .in11({{31{1'b0}}, comparator_1_lt[0]}),
    .in12({{31{1'b0}}, comparator_2_lt[0]}), .in13({32{1'b0}}), .in14({32{1'b0}}), .in15({32{1'b0}}),
    .out(Result), .sel(AluOP));
  Multiplexer #(.select(4), .width(32), .enable("false")) multiplexer_2 (
    .in0({32{1'b0}}), .in1({32{1'b0}}), .in2({32{1'b0}}), .in3(multiplier_1_cout), .in4(divider_1_rem),
    .in5({32{1'b0}}), .in6({32{1'b0}}), .in7({32{1'b0}}), .in8({32{1'b0}}), .in9({32{1'b0}}),
    .in10({32{1'b0}}), .in11({32{1'b0}}), .in12({32{1'b0}}), .in13({32{1'b0}}), .in14({32{1'b0}}),
    .in15({32{1'b0}}), .out(Result_2), .sel(AluOP));

  // Other names for the same wires on the sheet: Result2[31:0] = Result_2; S[3:0] = AluOP

  // Notes on the sheet:
  //   不要改变此引脚区域内容，也不要改变ALU封装形式
  //   输入引脚
  //   输出引脚
endmodule

module ALUOP (
  input  F5,
  input  F4,
  input  F3,
  input  F2,
  input  F1,
  input  F0,
  output A3,
  output A2,
  output A1,
  output A0
);

  wire and_2_out, and_3_out, and_4_out, and_5_out, and_6_out, and_7_out, and_8_out, and_9_out, and_10_out,
       and_11_out, and_12_out, not_1_out, not_2_out, not_3_out, not_4_out, not_5_out, not_6_out, not_7_out,
       not_8_out, not_9_out, not_10_out, not_11_out, not_12_out, not_13_out;

  and and_1 (A3, F5, F1);
  and and_2 (and_2_out, F4, F1);
  and and_3 (and_3_out, F5, not_1_out);
  not not_1 (not_1_out, F1);
  not not_2 (not_2_out, F5);
  not not_3 (not_3_out, F3);
  not not_4 (not_4_out, F0);
  not not_5 (not_5_out, F3);
  not not_6 (not_6_out, F1);
  not not_7 (not_7_out, F1);
  not not_8 (not_8_out, F5);
  and and_4 (and_4_out, not_8_out, not_9_out, F0);
  not not_9 (not_9_out, F4);
  not not_10 (not_10_out, F4);
  and and_5 (and_5_out, not_10_out, not_11_out, F0);
  not not_11 (not_11_out, F2);
  and and_6 (and_6_out, F4, not_12_out);
  not not_12 (not_12_out, F1);
  and and_7 (and_7_out, F5, not_13_out);
  not not_13 (not_13_out, F0);
  or or_1 (A2, and_2_out, and_3_out);
  and and_8 (and_8_out, not_2_out, not_3_out, F1, not_4_out);
  and and_9 (and_9_out, F4, not_5_out);
  and and_10 (and_10_out, F4, not_6_out);
  and and_11 (and_11_out, F5, F1, F0);
  and and_12 (and_12_out, F5, F2, not_7_out);
  or or_2 (A0, and_4_out, and_5_out, and_6_out, and_7_out);
  or or_3 (A1, and_8_out, and_9_out, and_10_out, and_11_out, and_12_out);
endmodule

module ALUOP1 (
  input  P5,
  input  P4,
  input  P3,
  input  P2,
  input  P1,
  input  P0,
  input  F5,
  input  F4,
  input  F3,
  input  F2,
  input  F1,
  input  F0,
  output ALU3,
  output ALU2,
  output ALU1,
  output ALU0,
  output ALUSrcX,
  output ALUSrcY1,
  output ALUSrcY0,
  output decode_rd,
  output NPCSrc1,
  output NPCSrc0,
  output extend1,
  output extend0
);

  wire and_1_out, and_2_out, and_3_out, and_4_out, and_5_out, and_6_out, and_7_out, and_8_out, and_9_out,
       and_10_out, and_11_out, and_12_out, and_13_out, and_14_out, and_15_out, and_16_out, and_17_out,
       and_18_out, and_19_out, and_20_out, and_21_out, and_22_out, and_23_out, and_24_out, and_25_out,
       and_26_out, and_27_out, and_28_out, and_29_out, and_30_out, and_31_out, and_32_out, and_33_out,
       and_34_out, and_35_out, and_36_out, and_37_out, and_38_out, and_39_out, and_40_out, and_41_out,
       and_42_out, and_43_out, and_44_out, and_45_out, and_46_out, and_47_out, and_48_out, and_49_out,
       and_50_out, and_51_out, and_52_out, and_53_out, and_54_out, and_55_out, and_56_out, and_57_out,
       and_58_out, and_59_out, and_60_out, and_61_out, and_62_out, and_63_out, and_64_out, and_65_out,
       and_66_out, and_67_out, and_68_out, and_69_out, and_70_out, and_71_out, and_72_out, and_73_out,
       and_74_out, and_75_out, and_76_out, and_77_out, and_78_out, and_79_out, and_80_out, and_81_out,
       and_82_out, and_83_out, and_86_out, and_87_out, and_88_out, and_89_out, and_90_out, and_91_out,
       and_92_out, and_93_out, and_94_out, and_95_out, and_96_out, and_97_out, and_98_out, and_99_out,
       not_1_out, not_2_out, not_3_out, not_4_out, not_5_out, not_6_out, not_7_out, not_8_out, not_9_out,
       not_10_out, not_11_out, not_12_out, not_13_out, not_14_out, not_15_out, not_16_out, not_17_out,
       not_18_out, not_19_out, not_20_out, not_21_out, not_22_out, not_23_out, not_24_out, not_25_out,
       not_26_out, not_27_out, not_28_out, not_29_out, not_30_out, not_31_out, not_32_out, not_33_out,
       not_34_out, not_35_out, not_36_out, not_37_out, not_38_out, not_39_out, not_40_out, not_41_out,
       not_42_out, not_43_out, not_44_out, not_45_out, not_46_out, not_47_out, not_48_out, not_49_out,
       not_50_out, not_51_out, not_52_out, not_53_out, not_54_out, not_55_out, not_56_out, not_57_out,
       not_58_out, not_59_out, not_60_out, not_61_out, not_62_out, not_63_out, not_64_out, not_65_out,
       not_66_out, not_67_out, not_68_out, not_69_out, not_70_out, not_71_out, not_72_out, not_73_out,
       not_74_out, not_75_out, not_76_out, not_77_out, not_78_out, not_79_out, not_80_out, not_81_out,
       not_82_out, not_83_out, not_84_out, not_85_out, not_86_out, not_87_out, not_88_out, not_89_out,
       not_90_out, not_91_out, not_92_out, not_93_out, not_94_out, not_95_out, not_96_out, not_97_out,
       not_98_out, not_99_out, not_100_out, not_101_out, not_102_out, not_103_out, not_104_out, not_105_out,
       not_106_out, not_107_out, not_108_out, not_109_out, not_110_out, not_111_out, not_112_out,
       not_113_out, not_114_out, not_115_out, not_116_out, not_117_out, not_118_out, not_119_out,
       not_120_out, not_121_out, not_122_out, not_123_out, not_124_out, not_125_out, not_126_out,
       not_127_out, not_128_out, not_129_out, not_130_out, not_131_out, not_132_out, not_133_out,
       not_134_out, not_135_out, not_136_out, not_137_out, not_138_out, not_139_out, not_140_out,
       not_141_out, not_142_out, not_143_out, not_144_out, not_145_out, not_146_out, not_147_out,
       not_148_out, not_149_out, not_150_out, not_151_out, not_152_out, not_153_out, not_154_out,
       not_155_out, not_156_out, not_157_out, not_158_out, not_159_out, not_160_out, not_161_out,
       not_162_out, not_163_out, not_164_out, not_165_out, not_166_out, not_167_out, not_168_out,
       not_169_out, not_170_out, not_171_out, not_172_out, not_173_out, not_174_out, not_175_out,
       not_176_out, not_177_out, not_178_out, not_179_out, not_180_out, not_181_out, not_182_out,
       not_183_out, not_184_out, not_185_out, not_186_out, not_187_out, not_188_out, not_189_out,
       not_190_out, not_191_out, not_192_out, not_193_out, not_194_out, not_195_out, not_196_out,
       not_197_out, not_198_out, not_199_out, not_200_out, not_201_out, not_202_out, not_203_out,
       not_204_out, not_205_out, not_206_out, not_207_out, not_208_out, not_209_out, not_210_out,
       not_211_out, not_212_out, not_213_out, not_214_out, not_215_out, not_216_out, not_217_out,
       not_218_out, not_219_out, not_220_out, not_221_out, not_222_out, not_223_out, not_224_out,
       not_225_out, not_226_out, not_227_out, not_228_out, not_229_out, not_230_out, not_231_out,
       not_232_out, not_233_out, not_234_out, not_235_out, not_236_out, not_237_out, not_238_out,
       not_239_out, not_240_out, not_241_out, not_242_out, not_243_out, not_244_out, not_245_out,
       not_246_out, not_247_out, not_248_out, not_249_out, not_250_out, not_251_out, not_252_out,
       not_253_out, not_254_out, not_255_out, not_256_out, not_257_out, not_258_out, not_259_out,
       not_260_out, not_261_out, not_262_out, not_263_out, not_264_out, not_265_out, not_266_out,
       not_267_out, not_268_out, not_269_out, not_270_out, not_271_out, not_272_out, not_273_out,
       not_274_out, not_275_out, not_276_out, not_277_out, not_278_out, not_279_out, not_280_out,
       not_281_out, not_282_out, not_283_out, not_284_out, not_285_out, not_286_out, not_287_out,
       not_288_out, not_289_out, not_290_out, not_291_out, not_292_out, not_293_out, not_294_out,
       not_295_out, not_296_out, not_297_out, not_298_out, not_299_out, not_300_out, not_301_out,
       not_302_out, not_303_out, not_304_out, not_305_out, not_306_out, not_307_out, not_308_out,
       not_309_out, not_310_out, not_311_out, not_312_out, not_313_out, not_314_out, not_315_out,
       not_316_out, not_317_out, not_318_out, not_319_out, not_320_out, not_321_out, not_322_out,
       not_323_out, not_324_out, not_325_out, not_326_out, not_327_out, not_328_out, not_329_out,
       not_330_out, not_331_out, not_332_out, not_333_out, not_334_out, not_335_out, not_336_out,
       not_337_out, not_338_out, not_339_out, not_340_out, not_341_out, not_342_out, not_343_out,
       not_344_out, not_345_out, not_346_out, not_347_out, not_348_out, not_349_out, not_350_out,
       not_351_out, not_352_out, not_353_out, not_354_out, not_355_out, not_356_out, not_357_out,
       not_358_out, not_359_out, not_360_out, not_361_out, not_362_out, not_363_out, not_364_out,
       not_365_out, not_366_out, not_367_out, not_368_out, not_369_out, not_370_out, not_371_out,
       not_372_out, not_373_out, not_374_out, not_375_out, not_376_out, not_377_out, not_378_out,
       not_379_out, not_380_out, not_381_out, not_382_out, not_383_out, not_384_out, not_385_out,
       not_386_out, not_387_out, not_388_out, not_389_out, not_390_out, not_391_out, not_392_out,
       not_393_out, not_394_out, not_395_out, not_396_out, not_397_out, not_398_out, not_399_out,
       not_400_out, not_401_out, not_402_out, not_403_out, not_404_out, not_405_out, not_406_out,
       not_407_out, not_408_out, not_409_out, not_410_out, not_411_out, not_412_out, not_413_out,
       not_414_out, not_415_out, not_416_out, not_417_out, or_1_out, or_2_out, or_3_out, or_4_out, or_5_out,
       or_9_out, or_11_out;

  not not_1 (not_1_out, F4);
  not not_2 (not_2_out, F3);
  not not_3 (not_3_out, F1);
  not not_4 (not_4_out, F4);
  not not_5 (not_5_out, F3);
  not not_6 (not_6_out, F4);
  not not_7 (not_7_out, F2);
  not not_8 (not_8_out, F0);
  not not_9 (not_9_out, F4);
  not not_10 (not_10_out, F2);
  not not_11 (not_11_out, F5);
  not not_12 (not_12_out, F4);
  not not_13 (not_13_out, F1);
  not not_14 (not_14_out, F0);
  not not_15 (not_15_out, F4);
  not not_16 (not_16_out, F3);
  not not_17 (not_17_out, F0);
  not not_18 (not_18_out, F4);
  not not_19 (not_19_out, F3);
  not not_20 (not_20_out, F2);
  not not_21 (not_21_out, F1);
  not not_22 (not_22_out, F0);
  not not_23 (not_23_out, F4);
  not not_24 (not_24_out, F3);
  not not_25 (not_25_out, F2);
  not not_26 (not_26_out, F1);
  not not_27 (not_27_out, F4);
  not not_28 (not_28_out, F3);
  not not_29 (not_29_out, F1);
  not not_30 (not_30_out, F0);
  not not_31 (not_31_out, F4);
  not not_32 (not_32_out, F3);
  not not_33 (not_33_out, F2);
  not not_34 (not_34_out, F0);
  not not_35 (not_35_out, F4);
  not not_36 (not_36_out, F2);
  not not_37 (not_37_out, F4);
  not not_38 (not_38_out, F3);
  not not_39 (not_39_out, F1);
  not not_40 (not_40_out, F0);
  not not_41 (not_41_out, F5);
  not not_42 (not_42_out, F4);
  not not_43 (not_43_out, F3);
  not not_44 (not_44_out, F2);
  not not_45 (not_45_out, F0);
  not not_46 (not_46_out, F4);
  not not_47 (not_47_out, F3);
  not not_48 (not_48_out, F2);
  not not_49 (not_49_out, F0);
  not not_50 (not_50_out, F4);
  not not_51 (not_51_out, F3);
  not not_52 (not_52_out, F4);
  not not_53 (not_53_out, F2);
  not not_54 (not_54_out, F0);
  not not_55 (not_55_out, F5);
  not not_56 (not_56_out, F4);
  not not_57 (not_57_out, F1);
  not not_58 (not_58_out, F0);
  not not_59 (not_59_out, F4);
  not not_60 (not_60_out, F3);
  not not_61 (not_61_out, F2);
  not not_62 (not_62_out, F1);
  not not_63 (not_63_out, F0);
  not not_64 (not_64_out, F4);
  not not_65 (not_65_out, F3);
  not not_66 (not_66_out, F2);
  not not_67 (not_67_out, F1);
  not not_68 (not_68_out, F4);
  not not_69 (not_69_out, F3);
  not not_70 (not_70_out, F1);
  not not_71 (not_71_out, F0);
  not not_72 (not_72_out, F5);
  not not_73 (not_73_out, F4);
  not not_74 (not_74_out, F3);
  not not_75 (not_75_out, F2);
  not not_76 (not_76_out, F4);
  not not_77 (not_77_out, F2);
  not not_78 (not_78_out, F0);
  not not_79 (not_79_out, F5);
  not not_80 (not_80_out, F4);
  not not_81 (not_81_out, F1);
  not not_82 (not_82_out, F0);
  not not_83 (not_83_out, F5);
  not not_84 (not_84_out, F4);
  not not_85 (not_85_out, F3);
  not not_86 (not_86_out, F4);
  not not_87 (not_87_out, F3);
  not not_88 (not_88_out, F0);
  not not_89 (not_89_out, F5);
  not not_90 (not_90_out, F4);
  not not_91 (not_91_out, F3);
  not not_92 (not_92_out, F2);
  not not_93 (not_93_out, F1);
  not not_94 (not_94_out, F0);
  not not_95 (not_95_out, F5);
  not not_96 (not_96_out, F4);
  not not_97 (not_97_out, F3);
  not not_98 (not_98_out, F2);
  not not_99 (not_99_out, F5);
  not not_100 (not_100_out, F4);
  not not_101 (not_101_out, F3);
  not not_102 (not_102_out, F2);
  not not_103 (not_103_out, F0);
  not not_104 (not_104_out, F5);
  not not_105 (not_105_out, F4);
  not not_106 (not_106_out, F3);
  not not_107 (not_107_out, P5);
  not not_108 (not_108_out, P4);
  not not_109 (not_109_out, P3);
  not not_110 (not_110_out, P2);
  not not_111 (not_111_out, P1);
  not not_112 (not_112_out, P0);
  not not_113 (not_113_out, F5);
  not not_114 (not_114_out, F4);
  not not_115 (not_115_out, F1);
  not not_116 (not_116_out, F0);
  not not_117 (not_117_out, P5);
  not not_118 (not_118_out, P4);
  not not_119 (not_119_out, P3);
  not not_120 (not_120_out, P2);
  not not_121 (not_121_out, P1);
  not not_122 (not_122_out, F4);
  not not_123 (not_123_out, F3);
  not not_124 (not_124_out, F2);
  not not_125 (not_125_out, F1);
  not not_126 (not_126_out, F0);
  not not_127 (not_127_out, F4);
  not not_128 (not_128_out, F3);
  not not_129 (not_129_out, F2);
  not not_130 (not_130_out, F1);
  not not_131 (not_131_out, F4);
  not not_132 (not_132_out, F3);
  not not_133 (not_133_out, F1);
  not not_134 (not_134_out, F0);
  not not_135 (not_135_out, F4);
  not not_136 (not_136_out, F3);
  not not_137 (not_137_out, F2);
  not not_138 (not_138_out, F0);
  not not_139 (not_139_out, F4);
  not not_140 (not_140_out, F3);
  not not_141 (not_141_out, F1);
  not not_142 (not_142_out, F4);
  not not_143 (not_143_out, F3);
  not not_144 (not_144_out, F4);
  not not_145 (not_145_out, F2);
  not not_146 (not_146_out, F0);
  not not_147 (not_147_out, F4);
  not not_148 (not_148_out, F2);
  not not_149 (not_149_out, F5);
  not not_150 (not_150_out, F4);
  not not_151 (not_151_out, F1);
  not not_152 (not_152_out, F0);
  not not_153 (not_153_out, F4);
  not not_154 (not_154_out, F3);
  not not_155 (not_155_out, F0);
  not not_156 (not_156_out, P5);
  not not_157 (not_157_out, P4);
  not not_158 (not_158_out, P2);
  not not_159 (not_159_out, P1);
  not not_160 (not_160_out, P0);
  not not_161 (not_161_out, P5);
  not not_162 (not_162_out, P4);
  not not_163 (not_163_out, P2);
  not not_164 (not_164_out, P1);
  not not_165 (not_165_out, P5);
  not not_166 (not_166_out, P4);
  not not_167 (not_167_out, P1);
  not not_168 (not_168_out, P0);
  not not_169 (not_169_out, P5);
  not not_170 (not_170_out, P4);
  not not_171 (not_171_out, P1);
  not not_172 (not_172_out, P4);
  not not_173 (not_173_out, P3);
  not not_174 (not_174_out, P2);
  not not_175 (not_175_out, P5);
  not not_176 (not_176_out, P4);
  not not_177 (not_177_out, P2);
  not not_178 (not_178_out, P0);
  not not_179 (not_179_out, P4);
  not not_180 (not_180_out, P3);
  not not_181 (not_181_out, P1);
  not not_182 (not_182_out, P5);
  not not_183 (not_183_out, P4);
  not not_184 (not_184_out, P3);
  not not_185 (not_185_out, P1);
  not not_186 (not_186_out, P0);
  not not_187 (not_187_out, P5);
  not not_188 (not_188_out, P4);
  not not_189 (not_189_out, P3);
  not not_190 (not_190_out, P1);
  not not_191 (not_191_out, P5);
  not not_192 (not_192_out, P4);
  not not_193 (not_193_out, P3);
  not not_194 (not_194_out, P2);
  not not_195 (not_195_out, P1);
  not not_196 (not_196_out, P5);
  not not_197 (not_197_out, P4);
  not not_198 (not_198_out, P3);
  not not_199 (not_199_out, P2);
  not not_200 (not_200_out, P0);
  not not_201 (not_201_out, P5);
  not not_202 (not_202_out, P4);
  not not_203 (not_203_out, P3);
  not not_204 (not_204_out, P2);
  not not_205 (not_205_out, P5);
  not not_206 (not_206_out, P4);
  not not_207 (not_207_out, P3);
  not not_208 (not_208_out, P2);
  not not_209 (not_209_out, P1);
  not not_210 (not_210_out, P0);
  not not_211 (not_211_out, F5);
  not not_212 (not_212_out, F4);
  not not_213 (not_213_out, F2);
  not not_214 (not_214_out, F1);
  not not_215 (not_215_out, F0);
  not not_216 (not_216_out, P5);
  not not_217 (not_217_out, P4);
  not not_218 (not_218_out, P3);
  not not_219 (not_219_out, P1);
  not not_220 (not_220_out, P0);
  not not_221 (not_221_out, P5);
  not not_222 (not_222_out, P4);
  not not_223 (not_223_out, P3);
  not not_224 (not_224_out, P1);
  not not_225 (not_225_out, P5);
  not not_226 (not_226_out, P4);
  not not_227 (not_227_out, P3);
  not not_228 (not_228_out, P2);
  not not_229 (not_229_out, P1);
  not not_230 (not_230_out, F5);
  not not_231 (not_231_out, F4);
  not not_232 (not_232_out, F3);
  not not_233 (not_233_out, F2);
  not not_234 (not_234_out, F1);
  not not_235 (not_235_out, F0);
  not not_236 (not_236_out, F5);
  not not_237 (not_237_out, F4);
  not not_238 (not_238_out, F3);
  not not_239 (not_239_out, F2);
  not not_240 (not_240_out, F5);
  not not_241 (not_241_out, F4);
  not not_242 (not_242_out, F3);
  not not_243 (not_243_out, F2);
  not not_244 (not_244_out, F0);
  not not_245 (not_245_out, F5);
  not not_246 (not_246_out, F4);
  not not_247 (not_247_out, F3);
  not not_248 (not_248_out, P5);
  not not_249 (not_249_out, P4);
  not not_250 (not_250_out, P3);
  not not_251 (not_251_out, P2);
  not not_252 (not_252_out, P1);
  not not_253 (not_253_out, P0);
  not not_254 (not_254_out, F5);
  not not_255 (not_255_out, F4);
  not not_256 (not_256_out, F3);
  not not_257 (not_257_out, P5);
  not not_258 (not_258_out, P4);
  not not_259 (not_259_out, P1);
  not not_260 (not_260_out, P0);
  not not_261 (not_261_out, P5);
  not not_262 (not_262_out, P4);
  not not_263 (not_263_out, P1);
  and and_1 (and_1_out, F5, not_1_out, not_2_out, F2, not_3_out, F0);
  and and_2 (and_2_out, F5, not_4_out, not_5_out, F2, F1, F0);
  and and_3 (and_3_out, F5, not_6_out, F3, not_7_out, F1, not_8_out);
  and and_4 (and_4_out, F5, not_9_out, F3, not_10_out, F1, F0);
  and and_5 (and_5_out, not_11_out, not_12_out, F3, F2, not_13_out, not_14_out);
  and and_6 (and_6_out, F5, not_15_out, not_16_out, F2, F1, not_17_out);
  and and_7 (and_7_out, F5, not_18_out, not_19_out, not_20_out, not_21_out, not_22_out);
  and and_8 (and_8_out, F5, not_23_out, not_24_out, not_25_out, not_26_out, F0);
  and and_9 (and_9_out, F5, not_27_out, not_28_out, F2, not_29_out, not_30_out);
  and and_10 (and_10_out, F5, not_31_out, not_32_out, not_33_out, F1, not_34_out);
  and and_11 (and_11_out, F5, not_35_out, F3, not_36_out, F1, F0);
  and and_12 (and_12_out, F5, not_37_out, not_38_out, F2, not_39_out, not_40_out);
  and and_13 (and_13_out, not_41_out, not_42_out, not_43_out, not_44_out, F1, not_45_out);
  and and_14 (and_14_out, F5, not_46_out, not_47_out, not_48_out, F1, not_49_out);
  and and_15 (and_15_out, F5, not_50_out, not_51_out, F2, F1, F0);
  and and_16 (and_16_out, F5, not_52_out, F3, not_53_out, F1, not_54_out);
  and and_17 (and_17_out, not_55_out, not_56_out, F3, F2, not_57_out, not_58_out);
  and and_18 (and_18_out, F5, not_59_out, not_60_out, not_61_out, not_62_out, not_63_out);
  and and_19 (and_19_out, F5, not_64_out, not_65_out, not_66_out, not_67_out, F0);
  and and_20 (and_20_out, F5, not_68_out, not_69_out, F2, not_70_out, not_71_out);
  and and_21 (and_21_out, not_72_out, not_73_out, not_74_out, not_75_out, F1, F0);
  and and_22 (and_22_out, F5, not_76_out, F3, not_77_out, F1, not_78_out);
  and and_23 (and_23_out, not_79_out, not_80_out, F3, F2, not_81_out, not_82_out);
  and and_24 (and_24_out, not_83_out, not_84_out, not_85_out, F2, F1, F0);
  and and_25 (and_25_out, F5, not_86_out, not_87_out, F2, F1, not_88_out);
  and and_26 (and_26_out, not_89_out, not_90_out, not_91_out, not_92_out, not_93_out, not_94_out);
  and and_27 (and_27_out, not_95_out, not_96_out, not_97_out, not_98_out, F1, F0);
  and and_28 (and_28_out, not_99_out, not_100_out, not_101_out, not_102_out, F1, not_103_out);
  and and_29 (and_29_out, not_104_out, not_105_out, not_106_out, F2, F1, F0);
  and and_30 (and_30_out, F5, not_122_out, not_123_out, not_124_out, not_125_out, not_126_out);
  and and_31 (and_31_out, F5, not_127_out, not_128_out, not_129_out, not_130_out, F0);
  and and_32 (and_32_out, F5, not_131_out, not_132_out, F2, not_133_out, not_134_out);
  and and_33 (and_33_out, F5, not_135_out, not_136_out, not_137_out, F1, not_138_out);
  and and_34 (and_34_out, F5, not_139_out, not_140_out, F2, not_141_out, F0);
  and and_35 (and_35_out, F5, not_142_out, not_143_out, F2, F1, F0);
  and and_36 (and_36_out, F5, not_144_out, F3, not_145_out, F1, not_146_out);
  and and_37 (and_37_out, F5, not_147_out, F3, not_148_out, F1, F0);
  and and_38 (and_38_out, not_149_out, not_150_out, F3, F2, not_151_out, not_152_out);
  and and_39 (and_39_out, F5, not_153_out, not_154_out, F2, F1, not_155_out);
  and and_40 (and_40_out, not_156_out, not_157_out, P3, not_158_out, not_159_out, not_160_out);
  and and_41 (and_41_out, not_161_out, not_162_out, P3, not_163_out, not_164_out, P0);
  and and_42 (and_42_out, not_165_out, not_166_out, P3, P2, not_167_out, not_168_out);
  and and_43 (and_43_out, not_169_out, not_170_out, P3, P2, not_171_out, P0);
  and and_44 (and_44_out, P5, not_172_out, not_173_out, not_174_out, P1, P0);
  and and_45 (and_45_out, not_175_out, not_176_out, P3, not_177_out, P1, not_178_out);
  and and_46 (and_46_out, P5, not_179_out, not_180_out, P2, not_181_out, P0);
  and and_47 (and_47_out, not_182_out, not_183_out, not_184_out, P2, not_185_out, not_186_out);
  and and_48 (and_48_out, not_187_out, not_188_out, not_189_out, P2, not_190_out, P0);
  and and_49 (and_49_out, not_191_out, not_192_out, not_193_out, not_194_out, not_195_out, P0);
  and and_50 (and_50_out, not_196_out, not_197_out, not_198_out, not_199_out, P1, not_200_out);
  and and_51 (and_51_out, not_201_out, not_202_out, not_203_out, not_204_out, P1, P0);
  and and_52 (and_52_out, not_230_out, not_231_out, not_232_out, not_233_out, not_234_out, not_235_out);
  and and_53 (and_53_out, not_236_out, not_237_out, not_238_out, not_239_out, F1, F0);
  and and_54 (and_54_out, not_240_out, not_241_out, not_242_out, not_243_out, F1, not_244_out);
  and and_55 (and_55_out, not_245_out, not_246_out, not_247_out, F2, F1, F0);
  not not_264 (not_264_out, P5);
  not not_265 (not_265_out, P4);
  not not_266 (not_266_out, P3);
  not not_267 (not_267_out, P2);
  not not_268 (not_268_out, P1);
  not not_269 (not_269_out, P0);
  or or_1 (or_1_out, and_1_out, and_2_out, and_3_out, and_4_out, and_5_out, and_6_out);
  not not_270 (not_270_out, P5);
  not not_271 (not_271_out, P4);
  not not_272 (not_272_out, P1);
  not not_273 (not_273_out, P5);
  not not_274 (not_274_out, P4);
  not not_275 (not_275_out, P3);
  not not_276 (not_276_out, P1);
  not not_277 (not_277_out, P0);
  not not_278 (not_278_out, P5);
  not not_279 (not_279_out, P4);
  not not_280 (not_280_out, P3);
  not not_281 (not_281_out, P1);
  not not_282 (not_282_out, P5);
  not not_283 (not_283_out, P4);
  not not_284 (not_284_out, P2);
  not not_285 (not_285_out, P0);
  not not_286 (not_286_out, P5);
  not not_287 (not_287_out, P4);
  not not_288 (not_288_out, P3);
  not not_289 (not_289_out, P2);
  not not_290 (not_290_out, P1);
  not not_291 (not_291_out, P5);
  not not_292 (not_292_out, P4);
  not not_293 (not_293_out, P3);
  not not_294 (not_294_out, P2);
  not not_295 (not_295_out, P1);
  not not_296 (not_296_out, P0);
  or or_2 (or_2_out, and_7_out, and_8_out, and_9_out, and_10_out, and_11_out);
  not not_297 (not_297_out, P5);
  not not_298 (not_298_out, P4);
  not not_299 (not_299_out, P2);
  not not_300 (not_300_out, P1);
  not not_301 (not_301_out, P0);
  not not_302 (not_302_out, P5);
  not not_303 (not_303_out, P4);
  not not_304 (not_304_out, P2);
  not not_305 (not_305_out, P1);
  not not_306 (not_306_out, P5);
  not not_307 (not_307_out, P4);
  not not_308 (not_308_out, P1);
  not not_309 (not_309_out, P0);
  not not_310 (not_310_out, P4);
  not not_311 (not_311_out, P3);
  not not_312 (not_312_out, P2);
  not not_313 (not_313_out, P4);
  not not_314 (not_314_out, P2);
  not not_315 (not_315_out, P4);
  not not_316 (not_316_out, P3);
  not not_317 (not_317_out, P1);
  not not_318 (not_318_out, P5);
  not not_319 (not_319_out, P4);
  not not_320 (not_320_out, P3);
  not not_321 (not_321_out, P2);
  not not_322 (not_322_out, P1);
  not not_323 (not_323_out, P0);
  or or_3 (or_3_out, and_12_out, and_13_out, and_14_out, and_15_out, and_16_out, and_17_out);
  not not_324 (not_324_out, P5);
  not not_325 (not_325_out, P4);
  not not_326 (not_326_out, P1);
  not not_327 (not_327_out, P0);
  not not_328 (not_328_out, P5);
  not not_329 (not_329_out, P4);
  not not_330 (not_330_out, P3);
  not not_331 (not_331_out, P1);
  not not_332 (not_332_out, P0);
  not not_333 (not_333_out, P5);
  not not_334 (not_334_out, P4);
  not not_335 (not_335_out, P3);
  not not_336 (not_336_out, P1);
  not not_337 (not_337_out, P5);
  not not_338 (not_338_out, P4);
  not not_339 (not_339_out, P2);
  not not_340 (not_340_out, P0);
  not not_341 (not_341_out, P5);
  not not_342 (not_342_out, P4);
  not not_343 (not_343_out, P3);
  not not_344 (not_344_out, P2);
  not not_345 (not_345_out, P1);
  not not_346 (not_346_out, P5);
  not not_347 (not_347_out, P4);
  not not_348 (not_348_out, P3);
  not not_349 (not_349_out, P2);
  not not_350 (not_350_out, P1);
  not not_351 (not_351_out, P0);
  or or_4 (or_4_out, and_18_out, and_19_out, and_20_out, and_21_out, and_22_out, and_23_out, and_24_out, and_25_out);
  not not_352 (not_352_out, P5);
  not not_353 (not_353_out, P4);
  not not_354 (not_354_out, P2);
  not not_355 (not_355_out, P1);
  not not_356 (not_356_out, P0);
  not not_357 (not_357_out, P5);
  not not_358 (not_358_out, P4);
  not not_359 (not_359_out, P2);
  not not_360 (not_360_out, P1);
  not not_361 (not_361_out, P5);
  not not_362 (not_362_out, P4);
  not not_363 (not_363_out, P1);
  not not_364 (not_364_out, P0);
  not not_365 (not_365_out, P4);
  not not_366 (not_366_out, P3);
  not not_367 (not_367_out, P2);
  not not_368 (not_368_out, P4);
  not not_369 (not_369_out, P2);
  not not_370 (not_370_out, P5);
  not not_371 (not_371_out, P4);
  not not_372 (not_372_out, P3);
  not not_373 (not_373_out, P1);
  not not_374 (not_374_out, P0);
  not not_375 (not_375_out, P5);
  not not_376 (not_376_out, P4);
  not not_377 (not_377_out, P3);
  not not_378 (not_378_out, P1);
  not not_379 (not_379_out, P5);
  not not_380 (not_380_out, P4);
  not not_381 (not_381_out, P2);
  not not_382 (not_382_out, P0);
  not not_383 (not_383_out, P4);
  not not_384 (not_384_out, P3);
  not not_385 (not_385_out, P1);
  not not_386 (not_386_out, P5);
  not not_387 (not_387_out, P4);
  not not_388 (not_388_out, P3);
  not not_389 (not_389_out, P2);
  not not_390 (not_390_out, P1);
  not not_391 (not_391_out, P5);
  not not_392 (not_392_out, P4);
  not not_393 (not_393_out, P3);
  not not_394 (not_394_out, P2);
  not not_395 (not_395_out, P1);
  not not_396 (not_396_out, P0);
  or or_5 (or_5_out, and_26_out, and_27_out, and_28_out, and_29_out);
  and and_56 (and_56_out, not_107_out, not_108_out, not_109_out, not_110_out, not_111_out, not_112_out, not_113_out, not_114_out, F3, F2, not_115_out, not_116_out);
  or or_6 (ALUSrcY1, and_56_out, and_57_out);
  and and_57 (and_57_out, not_117_out, not_118_out, not_119_out, not_120_out, not_121_out, P0);
  or or_7 (decode_rd, and_40_out, and_41_out, and_42_out, and_43_out, and_44_out, and_45_out, and_46_out);
  or or_8 (NPCSrc1, and_47_out, and_48_out, and_49_out, and_50_out, and_51_out);
  and and_58 (and_58_out, not_205_out, not_206_out, not_207_out, not_208_out, not_209_out, not_210_out, not_211_out, not_212_out, F3, not_213_out, not_214_out, not_215_out);
  and and_59 (and_59_out, not_216_out, not_217_out, not_218_out, P2, not_219_out, not_220_out);
  and and_60 (and_60_out, not_221_out, not_222_out, not_223_out, P2, not_224_out, P0);
  and and_61 (and_61_out, not_225_out, not_226_out, not_227_out, not_228_out, not_229_out, P0);
  not not_397 (not_397_out, P5);
  not not_398 (not_398_out, P4);
  not not_399 (not_399_out, P3);
  not not_400 (not_400_out, P2);
  not not_401 (not_401_out, P1);
  not not_402 (not_402_out, P0);
  or or_9 (or_9_out, and_52_out, and_53_out, and_54_out, and_55_out);
  and and_62 (and_62_out, not_248_out, not_249_out, not_250_out, not_251_out, not_252_out, not_253_out, not_254_out, not_255_out, not_256_out, F2, F1, F0);
  and and_63 (and_63_out, not_257_out, not_258_out, P3, P2, not_259_out, not_260_out);
  or or_10 (extend0, and_62_out, and_63_out, and_64_out);
  and and_64 (and_64_out, not_261_out, not_262_out, P3, P2, not_263_out, P0);
  and and_65 (and_65_out, not_264_out, not_265_out, not_266_out, not_267_out, not_268_out, not_269_out, or_1_out);
  and and_66 (and_66_out, not_270_out, not_271_out, P3, P2, not_272_out, P0);
  and and_67 (and_67_out, not_273_out, not_274_out, not_275_out, P2, not_276_out, not_277_out);
  and and_68 (and_68_out, not_278_out, not_279_out, not_280_out, P2, not_281_out, P0);
  and and_69 (and_69_out, not_282_out, not_283_out, P3, not_284_out, P1, not_285_out);
  and and_70 (and_70_out, not_286_out, not_287_out, not_288_out, not_289_out, not_290_out, P0);
  and and_71 (and_71_out, not_291_out, not_292_out, not_293_out, not_294_out, not_295_out, not_296_out, or_2_out);
  and and_72 (and_72_out, not_297_out, not_298_out, P3, not_299_out, not_300_out, not_301_out);
  and and_73 (and_73_out, not_302_out, not_303_out, P3, not_304_out, not_305_out, P0);
  and and_74 (and_74_out, not_306_out, not_307_out, P3, P2, not_308_out, not_309_out);
  and and_75 (and_75_out, P5, not_310_out, not_311_out, not_312_out, P1, P0);
  and and_76 (and_76_out, P5, not_313_out, P3, not_314_out, P1, P0);
  and and_77 (and_77_out, P5, not_315_out, not_316_out, P2, not_317_out, P0);
  and and_78 (and_78_out, not_318_out, not_319_out, not_320_out, not_321_out, not_322_out, not_323_out, or_3_out);
  and and_79 (and_79_out, not_324_out, not_325_out, P3, P2, not_326_out, not_327_out);
  and and_80 (and_80_out, not_328_out, not_329_out, not_330_out, P2, not_331_out, not_332_out);
  and and_81 (and_81_out, not_333_out, not_334_out, not_335_out, P2, not_336_out, P0);
  and and_82 (and_82_out, not_337_out, not_338_out, P3, not_339_out, P1, not_340_out);
  and and_83 (and_83_out, not_341_out, not_342_out, not_343_out, not_344_out, not_345_out, P0);
  and and_84 (ALUSrcX, not_391_out, not_392_out, not_393_out, not_394_out, not_395_out, not_396_out, or_5_out);
  not not_403 (not_403_out, P5);
  not not_404 (not_404_out, P4);
  not not_405 (not_405_out, P3);
  not not_406 (not_406_out, P2);
  not not_407 (not_407_out, P1);
  not not_408 (not_408_out, P0);
  or or_11 (or_11_out, and_30_out, and_31_out, and_32_out, and_33_out, and_34_out, and_35_out, and_36_out, and_37_out, and_38_out, and_39_out);
  not not_409 (not_409_out, P5);
  not not_410 (not_410_out, P4);
  not not_411 (not_411_out, P3);
  not not_412 (not_412_out, P1);
  not not_413 (not_413_out, P0);
  not not_414 (not_414_out, P5);
  not not_415 (not_415_out, P4);
  not not_416 (not_416_out, P3);
  not not_417 (not_417_out, P1);
  or or_12 (NPCSrc0, and_58_out, and_59_out, and_60_out, and_61_out);
  and and_85 (extend1, not_397_out, not_398_out, not_399_out, not_400_out, not_401_out, not_402_out, or_9_out);
  or or_13 (ALU2, and_71_out, and_72_out, and_73_out, and_74_out, and_75_out, and_76_out, and_77_out);
  and and_86 (and_86_out, not_346_out, not_347_out, not_348_out, not_349_out, not_350_out, not_351_out, or_4_out);
  and and_87 (and_87_out, not_352_out, not_353_out, P3, not_354_out, not_355_out, not_356_out);
  and and_88 (and_88_out, not_357_out, not_358_out, P3, not_359_out, not_360_out, P0);
  and and_89 (and_89_out, not_361_out, not_362_out, P3, P2, not_363_out, not_364_out);
  and and_90 (and_90_out, P5, not_365_out, not_366_out, not_367_out, P1, P0);
  and and_91 (and_91_out, P5, not_368_out, P3, not_369_out, P1, P0);
  and and_92 (and_92_out, not_370_out, not_371_out, not_372_out, P2, not_373_out, not_374_out);
  and and_93 (and_93_out, not_375_out, not_376_out, not_377_out, P2, not_378_out, P0);
  and and_94 (and_94_out, not_379_out, not_380_out, P3, not_381_out, P1, not_382_out);
  and and_95 (and_95_out, P5, not_383_out, not_384_out, P2, not_385_out, P0);
  and and_96 (and_96_out, not_386_out, not_387_out, not_388_out, not_389_out, not_390_out, P0);
  and and_97 (and_97_out, not_403_out, not_404_out, not_405_out, not_406_out, not_407_out, not_408_out, or_11_out);
  and and_98 (and_98_out, not_409_out, not_410_out, not_411_out, P2, not_412_out, not_413_out);
  and and_99 (and_99_out, not_414_out, not_415_out, not_416_out, P2, not_417_out, P0);
  or or_14 (ALU3, and_65_out, and_66_out, and_67_out, and_68_out, and_69_out, and_70_out);
  or or_15 (ALU1, and_78_out, and_79_out, and_80_out, and_81_out, and_82_out, and_83_out);
  or or_16 (ALU0, and_86_out, and_87_out, and_88_out, and_89_out, and_90_out, and_91_out, and_92_out, and_93_out, and_94_out, and_95_out, and_96_out);
  or or_17 (ALUSrcY0, and_97_out, and_98_out, and_99_out);
endmodule

module ALUOP2 (
  input  P5,
  input  P4,
  input  P3,
  input  P2,
  input  P1,
  input  P0,
  input  F5,
  input  F4,
  input  F3,
  input  F2,
  input  F1,
  input  F0,
  output ALU3,
  output ALU2,
  output ALU1,
  output ALU0
);

  wire and_1_out, and_2_out, and_3_out, and_4_out, and_5_out, and_6_out, and_7_out, and_8_out, and_9_out,
       and_10_out, and_11_out, and_12_out, and_13_out, and_14_out, and_15_out, and_16_out, and_17_out,
       and_18_out, and_19_out, and_20_out, and_21_out, and_22_out, and_23_out, and_24_out, and_25_out,
       and_26_out, and_27_out, and_28_out, and_29_out, and_30_out, and_31_out, and_32_out, and_33_out,
       and_34_out, and_35_out, and_36_out, and_37_out, and_38_out, and_39_out, and_40_out, and_41_out,
       and_42_out, and_43_out, and_44_out, and_45_out, and_46_out, and_47_out, and_48_out, and_49_out,
       and_50_out, and_51_out, and_52_out, and_53_out, and_54_out, and_55_out, not_1_out, not_2_out,
       not_3_out, not_4_out, not_5_out, not_6_out, not_7_out, not_8_out, not_9_out, not_10_out, not_11_out,
       not_12_out, not_13_out, not_14_out, not_15_out, not_16_out, not_17_out, not_18_out, not_19_out,
       not_20_out, not_21_out, not_22_out, not_23_out, not_24_out, not_25_out, not_26_out, not_27_out,
       not_28_out, not_29_out, not_30_out, not_31_out, not_32_out, not_33_out, not_34_out, not_35_out,
       not_36_out, not_37_out, not_38_out, not_39_out, not_40_out, not_41_out, not_42_out, not_43_out,
       not_44_out, not_45_out, not_46_out, not_47_out, not_48_out, not_49_out, not_50_out, not_51_out,
       not_52_out, not_53_out, not_54_out, not_55_out, not_56_out, not_57_out, not_58_out, not_59_out,
       not_60_out, not_61_out, not_62_out, not_63_out, not_64_out, not_65_out, not_66_out, not_67_out,
       not_68_out, not_69_out, not_70_out, not_71_out, not_72_out, not_73_out, not_74_out, not_75_out,
       not_76_out, not_77_out, not_78_out, not_79_out, not_80_out, not_81_out, not_82_out, not_83_out,
       not_84_out, not_85_out, not_86_out, not_87_out, not_88_out, not_89_out, not_90_out, not_91_out,
       not_92_out, not_93_out, not_94_out, not_95_out, not_96_out, not_97_out, not_98_out, not_99_out,
       not_100_out, not_101_out, not_102_out, not_103_out, not_104_out, not_105_out, not_106_out,
       not_107_out, not_108_out, not_109_out, not_110_out, not_111_out, not_112_out, not_113_out,
       not_114_out, not_115_out, not_116_out, not_117_out, not_118_out, not_119_out, not_120_out,
       not_121_out, not_122_out, not_123_out, not_124_out, not_125_out, not_126_out, not_127_out,
       not_128_out, not_129_out, not_130_out, not_131_out, not_132_out, not_133_out, not_134_out,
       not_135_out, not_136_out, not_137_out, not_138_out, not_139_out, not_140_out, not_141_out,
       not_142_out, not_143_out, not_144_out, not_145_out, not_146_out, not_147_out, not_148_out,
       not_149_out, not_150_out, not_151_out, not_152_out, not_153_out, not_154_out, not_155_out,
       not_156_out, not_157_out, not_158_out, not_159_out, not_160_out, not_161_out, not_162_out,
       not_163_out, not_164_out, not_165_out, not_166_out, not_167_out, not_168_out, not_169_out,
       not_170_out, not_171_out, not_172_out, not_173_out, not_174_out, not_175_out, not_176_out,
       not_177_out, not_178_out, not_179_out, not_180_out, not_181_out, not_182_out, not_183_out,
       not_184_out, not_185_out, not_186_out, not_187_out, not_188_out, not_189_out, not_190_out,
       not_191_out, not_192_out, not_193_out, not_194_out, not_195_out, not_196_out, not_197_out,
       not_198_out, not_199_out, not_200_out, not_201_out, not_202_out, not_203_out, not_204_out,
       not_205_out, not_206_out, not_207_out, not_208_out, not_209_out, not_210_out, not_211_out,
       not_212_out, not_213_out, not_214_out, not_215_out, or_1_out, or_2_out, or_3_out, or_4_out;

  not not_1 (not_1_out, F4);
  not not_2 (not_2_out, F3);
  not not_3 (not_3_out, F1);
  not not_4 (not_4_out, F4);
  not not_5 (not_5_out, F3);
  not not_6 (not_6_out, F4);
  not not_7 (not_7_out, F2);
  not not_8 (not_8_out, F0);
  not not_9 (not_9_out, F4);
  not not_10 (not_10_out, F2);
  not not_11 (not_11_out, F5);
  not not_12 (not_12_out, F4);
  not not_13 (not_13_out, F1);
  not not_14 (not_14_out, F0);
  not not_15 (not_15_out, F4);
  not not_16 (not_16_out, F3);
  not not_17 (not_17_out, F0);
  not not_18 (not_18_out, F4);
  not not_19 (not_19_out, F3);
  not not_20 (not_20_out, F2);
  not not_21 (not_21_out, F1);
  not not_22 (not_22_out, F0);
  not not_23 (not_23_out, F4);
  not not_24 (not_24_out, F3);
  not not_25 (not_25_out, F2);
  not not_26 (not_26_out, F1);
  not not_27 (not_27_out, F4);
  not not_28 (not_28_out, F3);
  not not_29 (not_29_out, F1);
  not not_30 (not_30_out, F0);
  not not_31 (not_31_out, F4);
  not not_32 (not_32_out, F3);
  not not_33 (not_33_out, F2);
  not not_34 (not_34_out, F0);
  not not_35 (not_35_out, F4);
  not not_36 (not_36_out, F2);
  not not_37 (not_37_out, F4);
  not not_38 (not_38_out, F3);
  not not_39 (not_39_out, F1);
  not not_40 (not_40_out, F0);
  not not_41 (not_41_out, F5);
  not not_42 (not_42_out, F4);
  not not_43 (not_43_out, F3);
  not not_44 (not_44_out, F2);
  not not_45 (not_45_out, F0);
  not not_46 (not_46_out, F4);
  not not_47 (not_47_out, F3);
  not not_48 (not_48_out, F2);
  not not_49 (not_49_out, F0);
  not not_50 (not_50_out, F4);
  not not_51 (not_51_out, F3);
  not not_52 (not_52_out, F4);
  not not_53 (not_53_out, F2);
  not not_54 (not_54_out, F0);
  not not_55 (not_55_out, F5);
  not not_56 (not_56_out, F4);
  not not_57 (not_57_out, F1);
  not not_58 (not_58_out, F0);
  not not_59 (not_59_out, F4);
  not not_60 (not_60_out, F3);
  not not_61 (not_61_out, F2);
  not not_62 (not_62_out, F1);
  not not_63 (not_63_out, F0);
  not not_64 (not_64_out, F4);
  not not_65 (not_65_out, F3);
  not not_66 (not_66_out, F2);
  not not_67 (not_67_out, F1);
  not not_68 (not_68_out, F4);
  not not_69 (not_69_out, F3);
  not not_70 (not_70_out, F1);
  not not_71 (not_71_out, F0);
  not not_72 (not_72_out, F5);
  not not_73 (not_73_out, F4);
  not not_74 (not_74_out, F3);
  not not_75 (not_75_out, F2);
  not not_76 (not_76_out, F4);
  not not_77 (not_77_out, F2);
  not not_78 (not_78_out, F0);
  not not_79 (not_79_out, F5);
  not not_80 (not_80_out, F4);
  not not_81 (not_81_out, F1);
  not not_82 (not_82_out, F0);
  not not_83 (not_83_out, F5);
  not not_84 (not_84_out, F4);
  not not_85 (not_85_out, F3);
  not not_86 (not_86_out, F4);
  not not_87 (not_87_out, F3);
  not not_88 (not_88_out, F0);
  and and_1 (and_1_out, F5, not_1_out, not_2_out, F2, not_3_out, F0);
  and and_2 (and_2_out, F5, not_4_out, not_5_out, F2, F1, F0);
  and and_3 (and_3_out, F5, not_6_out, F3, not_7_out, F1, not_8_out);
  and and_4 (and_4_out, F5, not_9_out, F3, not_10_out, F1, F0);
  and and_5 (and_5_out, not_11_out, not_12_out, F3, F2, not_13_out, not_14_out);
  and and_6 (and_6_out, F5, not_15_out, not_16_out, F2, F1, not_17_out);
  and and_7 (and_7_out, F5, not_18_out, not_19_out, not_20_out, not_21_out, not_22_out);
  and and_8 (and_8_out, F5, not_23_out, not_24_out, not_25_out, not_26_out, F0);
  and and_9 (and_9_out, F5, not_27_out, not_28_out, F2, not_29_out, not_30_out);
  and and_10 (and_10_out, F5, not_31_out, not_32_out, not_33_out, F1, not_34_out);
  and and_11 (and_11_out, F5, not_35_out, F3, not_36_out, F1, F0);
  and and_12 (and_12_out, F5, not_37_out, not_38_out, F2, not_39_out, not_40_out);
  and and_13 (and_13_out, not_41_out, not_42_out, not_43_out, not_44_out, F1, not_45_out);
  and and_14 (and_14_out, F5, not_46_out, not_47_out, not_48_out, F1, not_49_out);
  and and_15 (and_15_out, F5, not_50_out, not_51_out, F2, F1, F0);
  and and_16 (and_16_out, F5, not_52_out, F3, not_53_out, F1, not_54_out);
  and and_17 (and_17_out, not_55_out, not_56_out, F3, F2, not_57_out, not_58_out);
  and and_18 (and_18_out, F5, not_59_out, not_60_out, not_61_out, not_62_out, not_63_out);
  and and_19 (and_19_out, F5, not_64_out, not_65_out, not_66_out, not_67_out, F0);
  and and_20 (and_20_out, F5, not_68_out, not_69_out, F2, not_70_out, not_71_out);
  and and_21 (and_21_out, not_72_out, not_73_out, not_74_out, not_75_out, F1, F0);
  and and_22 (and_22_out, F5, not_76_out, F3, not_77_out, F1, not_78_out);
  and and_23 (and_23_out, not_79_out, not_80_out, F3, F2, not_81_out, not_82_out);
  and and_24 (and_24_out, not_83_out, not_84_out, not_85_out, F2, F1, F0);
  and and_25 (and_25_out, F5, not_86_out, not_87_out, F2, F1, not_88_out);
  not not_89 (not_89_out, P5);
  not not_90 (not_90_out, P4);
  not not_91 (not_91_out, P3);
  not not_92 (not_92_out, P2);
  not not_93 (not_93_out, P1);
  not not_94 (not_94_out, P0);
  or or_1 (or_1_out, and_1_out, and_2_out, and_3_out, and_4_out, and_5_out, and_6_out);
  not not_95 (not_95_out, P5);
  not not_96 (not_96_out, P4);
  not not_97 (not_97_out, P1);
  not not_98 (not_98_out, P5);
  not not_99 (not_99_out, P4);
  not not_100 (not_100_out, P3);
  not not_101 (not_101_out, P1);
  not not_102 (not_102_out, P0);
  not not_103 (not_103_out, P5);
  not not_104 (not_104_out, P4);
  not not_105 (not_105_out, P3);
  not not_106 (not_106_out, P1);
  not not_107 (not_107_out, P5);
  not not_108 (not_108_out, P4);
  not not_109 (not_109_out, P2);
  not not_110 (not_110_out, P0);
  not not_111 (not_111_out, P5);
  not not_112 (not_112_out, P4);
  not not_113 (not_113_out, P3);
  not not_114 (not_114_out, P2);
  not not_115 (not_115_out, P1);
  not not_116 (not_116_out, P5);
  not not_117 (not_117_out, P4);
  not not_118 (not_118_out, P3);
  not not_119 (not_119_out, P2);
  not not_120 (not_120_out, P1);
  not not_121 (not_121_out, P0);
  or or_2 (or_2_out, and_7_out, and_8_out, and_9_out, and_10_out, and_11_out);
  not not_122 (not_122_out, P5);
  not not_123 (not_123_out, P4);
  not not_124 (not_124_out, P2);
  not not_125 (not_125_out, P1);
  not not_126 (not_126_out, P0);
  not not_127 (not_127_out, P5);
  not not_128 (not_128_out, P4);
  not not_129 (not_129_out, P2);
  not not_130 (not_130_out, P1);
  not not_131 (not_131_out, P5);
  not not_132 (not_132_out, P4);
  not not_133 (not_133_out, P1);
  not not_134 (not_134_out, P0);
  not not_135 (not_135_out, P4);
  not not_136 (not_136_out, P3);
  not not_137 (not_137_out, P2);
  not not_138 (not_138_out, P4);
  not not_139 (not_139_out, P2);
  not not_140 (not_140_out, P4);
  not not_141 (not_141_out, P3);
  not not_142 (not_142_out, P1);
  not not_143 (not_143_out, P5);
  not not_144 (not_144_out, P4);
  not not_145 (not_145_out, P3);
  not not_146 (not_146_out, P2);
  not not_147 (not_147_out, P1);
  not not_148 (not_148_out, P0);
  or or_3 (or_3_out, and_12_out, and_13_out, and_14_out, and_15_out, and_16_out, and_17_out);
  not not_149 (not_149_out, P5);
  not not_150 (not_150_out, P4);
  not not_151 (not_151_out, P1);
  not not_152 (not_152_out, P0);
  not not_153 (not_153_out, P5);
  not not_154 (not_154_out, P4);
  not not_155 (not_155_out, P3);
  not not_156 (not_156_out, P1);
  not not_157 (not_157_out, P0);
  not not_158 (not_158_out, P5);
  not not_159 (not_159_out, P4);
  not not_160 (not_160_out, P3);
  not not_161 (not_161_out, P1);
  not not_162 (not_162_out, P5);
  not not_163 (not_163_out, P4);
  not not_164 (not_164_out, P2);
  not not_165 (not_165_out, P0);
  not not_166 (not_166_out, P5);
  not not_167 (not_167_out, P4);
  not not_168 (not_168_out, P3);
  not not_169 (not_169_out, P2);
  not not_170 (not_170_out, P1);
  not not_171 (not_171_out, P5);
  not not_172 (not_172_out, P4);
  not not_173 (not_173_out, P3);
  not not_174 (not_174_out, P2);
  not not_175 (not_175_out, P1);
  not not_176 (not_176_out, P0);
  or or_4 (or_4_out, and_18_out, and_19_out, and_20_out, and_21_out, and_22_out, and_23_out, and_24_out, and_25_out);
  not not_177 (not_177_out, P5);
  not not_178 (not_178_out, P4);
  not not_179 (not_179_out, P2);
  not not_180 (not_180_out, P1);
  not not_181 (not_181_out, P0);
  not not_182 (not_182_out, P5);
  not not_183 (not_183_out, P4);
  not not_184 (not_184_out, P2);
  not not_185 (not_185_out, P1);
  not not_186 (not_186_out, P5);
  not not_187 (not_187_out, P4);
  not not_188 (not_188_out, P1);
  not not_189 (not_189_out, P0);
  not not_190 (not_190_out, P4);
  not not_191 (not_191_out, P3);
  not not_192 (not_192_out, P2);
  not not_193 (not_193_out, P4);
  not not_194 (not_194_out, P2);
  not not_195 (not_195_out, P5);
  not not_196 (not_196_out, P4);
  not not_197 (not_197_out, P3);
  not not_198 (not_198_out, P1);
  not not_199 (not_199_out, P0);
  not not_200 (not_200_out, P5);
  not not_201 (not_201_out, P4);
  not not_202 (not_202_out, P3);
  not not_203 (not_203_out, P1);
  not not_204 (not_204_out, P5);
  not not_205 (not_205_out, P4);
  not not_206 (not_206_out, P2);
  not not_207 (not_207_out, P0);
  not not_208 (not_208_out, P4);
  not not_209 (not_209_out, P3);
  not not_210 (not_210_out, P1);
  not not_211 (not_211_out, P5);
  not not_212 (not_212_out, P4);
  not not_213 (not_213_out, P3);
  not not_214 (not_214_out, P2);
  not not_215 (not_215_out, P1);
  and and_26 (and_26_out, not_89_out, not_90_out, not_91_out, not_92_out, not_93_out, not_94_out, or_1_out);
  and and_27 (and_27_out, not_95_out, not_96_out, P3, P2, not_97_out, P0);
  and and_28 (and_28_out, not_98_out, not_99_out, not_100_out, P2, not_101_out, not_102_out);
  and and_29 (and_29_out, not_103_out, not_104_out, not_105_out, P2, not_106_out, P0);
  and and_30 (and_30_out, not_107_out, not_108_out, P3, not_109_out, P1, not_110_out);
  and and_31 (and_31_out, not_111_out, not_112_out, not_113_out, not_114_out, not_115_out, P0);
  and and_32 (and_32_out, not_116_out, not_117_out, not_118_out, not_119_out, not_120_out, not_121_out, or_2_out);
  and and_33 (and_33_out, not_122_out, not_123_out, P3, not_124_out, not_125_out, not_126_out);
  and and_34 (and_34_out, not_127_out, not_128_out, P3, not_129_out, not_130_out, P0);
  and and_35 (and_35_out, not_131_out, not_132_out, P3, P2, not_133_out, not_134_out);
  and and_36 (and_36_out, P5, not_135_out, not_136_out, not_137_out, P1, P0);
  and and_37 (and_37_out, P5, not_138_out, P3, not_139_out, P1, P0);
  and and_38 (and_38_out, P5, not_140_out, not_141_out, P2, not_142_out, P0);
  and and_39 (and_39_out, not_143_out, not_144_out, not_145_out, not_146_out, not_147_out, not_148_out, or_3_out);
  and and_40 (and_40_out, not_149_out, not_150_out, P3, P2, not_151_out, not_152_out);
  and and_41 (and_41_out, not_153_out, not_154_out, not_155_out, P2, not_156_out, not_157_out);
  and and_42 (and_42_out, not_158_out, not_159_out, not_160_out, P2, not_161_out, P0);
  and and_43 (and_43_out, not_162_out, not_163_out, P3, not_164_out, P1, not_165_out);
  and and_44 (and_44_out, not_166_out, not_167_out, not_168_out, not_169_out, not_170_out, P0);
  and and_45 (and_45_out, not_171_out, not_172_out, not_173_out, not_174_out, not_175_out, not_176_out, or_4_out);
  and and_46 (and_46_out, not_177_out, not_178_out, P3, not_179_out, not_180_out, not_181_out);
  and and_47 (and_47_out, not_182_out, not_183_out, P3, not_184_out, not_185_out, P0);
  and and_48 (and_48_out, not_186_out, not_187_out, P3, P2, not_188_out, not_189_out);
  and and_49 (and_49_out, P5, not_190_out, not_191_out, not_192_out, P1, P0);
  and and_50 (and_50_out, P5, not_193_out, P3, not_194_out, P1, P0);
  and and_51 (and_51_out, not_195_out, not_196_out, not_197_out, P2, not_198_out, not_199_out);
  and and_52 (and_52_out, not_200_out, not_201_out, not_202_out, P2, not_203_out, P0);
  and and_53 (and_53_out, not_204_out, not_205_out, P3, not_206_out, P1, not_207_out);
  and and_54 (and_54_out, P5, not_208_out, not_209_out, P2, not_210_out, P0);
  and and_55 (and_55_out, not_211_out, not_212_out, not_213_out, not_214_out, not_215_out, P0);
  or or_5 (ALU3, and_26_out, and_27_out, and_28_out, and_29_out, and_30_out, and_31_out);
  or or_6 (ALU2, and_32_out, and_33_out, and_34_out, and_35_out, and_36_out, and_37_out, and_38_out);
  or or_7 (ALU1, and_39_out, and_40_out, and_41_out, and_42_out, and_43_out, and_44_out);
  or or_8 (ALU0, and_45_out, and_46_out, and_47_out, and_48_out, and_49_out, and_50_out, and_51_out, and_52_out, and_53_out, and_54_out, and_55_out);
endmodule
